// Logisim project Lab_2 Summator.circ as structural Verilog: 6 circuits, main circuit Полусумматор
module \Полусумматор  (
  input  A,
  input  B,
  output Out,
  output P
);

  xor xor_1 (Out, A, B);
  and and_1 (P, A, B);
endmodule

module \Сумматор  (
  input  in_1,
  input  in_2,
  input  in_3,
  output out_4,
  output out_5
);

  wire \полусумматор_1_out , \полусумматор_1_p , \полусумматор_2_p ;

  \Полусумматор  \u_полусумматор_1  (.A(in_2), .B(in_3), .Out(\полусумматор_1_out ), .P(\полусумматор_1_p ));
  \Полусумматор  \u_полусумматор_2  (.A(in_1), .B(\полусумматор_1_out ), .Out(out_4), .P(\полусумматор_2_p ));
  or or_1 (out_5, \полусумматор_2_p , \полусумматор_1_p );
endmodule

module \Восьмибитный  (
  input  [7:0] in_1,
  input  [7:0] in_2,
  input  in_3
);

  wire \сумматор_1_out_5 , \сумматор_2_out_5 , \сумматор_3_out_5 , \сумматор_4_out_5 , \сумматор_5_out_5 ,
       \сумматор_6_out_5 , \сумматор_7_out_5 ;
  wire [8:0] \сумматор_1_out_4 ;

  // Probe on in_1
  // Probe on in_2
  // Probe on \сумматор_1_out_4 
  \Сумматор  \u_сумматор_1  (
    .in_1(in_3), .in_2(in_1[0]), .in_3(in_2[0]), .out_5(\сумматор_1_out_5 ), .out_4(\сумматор_1_out_4 [0]));
  \Сумматор  \u_сумматор_2  (
    .in_1(\сумматор_1_out_5 ), .in_2(in_1[1]), .in_3(in_2[1]), .out_5(\сумматор_2_out_5 ),
    .out_4(\сумматор_1_out_4 [1]));
  \Сумматор  \u_сумматор_3  (
    .in_1(\сумматор_2_out_5 ), .in_2(in_1[2]), .in_3(in_2[2]), .out_5(\сумматор_3_out_5 ),
    .out_4(\сумматор_1_out_4 [2]));
  \Сумматор  \u_сумматор_4  (
    .in_1(\сумматор_3_out_5 ), .in_2(in_1[3]), .in_3(in_2[3]), .out_5(\сумматор_4_out_5 ),
    .out_4(\сумматор_1_out_4 [3]));
  \Сумматор  \u_сумматор_5  (
    .in_1(\сумматор_4_out_5 ), .in_2(in_1[4]), .in_3(in_2[4]), .out_5(\сумматор_5_out_5 ),
    .out_4(\сумматор_1_out_4 [4]));
  \Сумматор  \u_сумматор_6  (
    .in_1(\сумматор_5_out_5 ), .in_2(in_1[5]), .in_3(in_2[5]), .out_5(\сумматор_6_out_5 ),
    .out_4(\сумматор_1_out_4 [5]));
  \Сумматор  \u_сумматор_7  (
    .in_1(\сумматор_6_out_5 ), .in_2(in_1[6]), .in_3(in_2[6]), .out_5(\сумматор_7_out_5 ),
    .out_4(\сумматор_1_out_4 [6]));
  \Сумматор  \u_сумматор_8  (
    .in_1(\сумматор_7_out_5 ), .in_2(in_1[7]), .in_3(in_2[7]), .out_5(\сумматор_1_out_4 [8]),
    .out_4(\сумматор_1_out_4 [7]));
  // Probe on \сумматор_1_out_4 

  // Notes on the sheet:
  //   +
  //   =
endmodule

module \Вычитатор  (
  input  [7:0] in_1,
  input  [7:0] in_2,
  input  in_3,
  output [8:0] out_4
);

  wire xor_1_out, xor_2_out, xor_3_out, xor_4_out, xor_5_out, xor_6_out, xor_7_out, xor_8_out,
       \сумматор_1_out_5 , \сумматор_2_out_5 , \сумматор_3_out_5 , \сумматор_4_out_5 , \сумматор_5_out_5 ,
       \сумматор_6_out_5 , \сумматор_7_out_5 , \сумматор_8_out_5 ;

  // Probe on in_1
  // Probe on in_2
  // Probe on out_4
  xor xor_1 (xor_1_out, in_3, in_2[7]);
  xor xor_2 (xor_2_out, in_3, in_2[6]);
  xor xor_3 (xor_3_out, in_3, in_2[5]);
  xor xor_4 (xor_4_out, in_3, in_2[4]);
  xor xor_5 (xor_5_out, in_3, in_2[3]);
  xor xor_6 (xor_6_out, in_3, in_2[1]);
  xor xor_7 (xor_7_out, in_3, in_2[2]);
  xor xor_8 (xor_8_out, in_3, in_2[0]);
  \Сумматор  \u_сумматор_1  (
    .in_1(in_3), .in_2(xor_8_out), .in_3(in_1[0]), .out_5(\сумматор_1_out_5 ), .out_4(out_4[0]));
  \Сумматор  \u_сумматор_2  (
    .in_1(\сумматор_1_out_5 ), .in_2(xor_6_out), .in_3(in_1[1]), .out_5(\сумматор_2_out_5 ), .out_4(out_4[1]));
  \Сумматор  \u_сумматор_3  (
    .in_1(\сумматор_2_out_5 ), .in_2(xor_7_out), .in_3(in_1[2]), .out_5(\сумматор_3_out_5 ), .out_4(out_4[2]));
  \Сумматор  \u_сумматор_4  (
    .in_1(\сумматор_3_out_5 ), .in_2(xor_5_out), .in_3(in_1[3]), .out_5(\сумматор_4_out_5 ), .out_4(out_4[3]));
  \Сумматор  \u_сумматор_5  (
    .in_1(\сумматор_4_out_5 ), .in_2(xor_4_out), .in_3(in_1[4]), .out_5(\сумматор_5_out_5 ), .out_4(out_4[4]));
  \Сумматор  \u_сумматор_6  (
    .in_1(\сумматор_5_out_5 ), .in_2(xor_3_out), .in_3(in_1[5]), .out_5(\сумматор_6_out_5 ), .out_4(out_4[5]));
  \Сумматор  \u_сумматор_7  (
    .in_1(\сумматор_6_out_5 ), .in_2(xor_2_out), .in_3(in_1[6]), .out_5(\сумматор_7_out_5 ), .out_4(out_4[6]));
  \Сумматор  \u_сумматор_8  (
    .in_1(\сумматор_7_out_5 ), .in_2(xor_1_out), .in_3(in_1[7]), .out_5(\сумматор_8_out_5 ), .out_4(out_4[7]));
  xor xor_9 (out_4[8], in_3, \сумматор_8_out_5 );

  // Notes on the sheet:
  //   А
  //   В
  //   -
  //   Из А вычесть В
  //   =
endmodule

module \Умножитель  (
  input  [3:0] in_1,
  input  [3:0] in_2
);

  wire and_1_out, and_2_out, and_3_out, and_4_out, and_5_out, and_6_out, and_7_out, and_8_out, and_9_out,
       and_10_out, and_11_out, and_12_out, and_13_out, and_14_out, and_15_out, \сумматор_2_out_4 ,
       \сумматор_2_out_5 , \сумматор_3_out_5 , \сумматор_4_out_4 , \сумматор_4_out_5 , \сумматор_5_out_5 ,
       \сумматор_6_out_4 , \сумматор_6_out_5 , \сумматор_7_out_5 , \сумматор_8_out_4 , \сумматор_8_out_5 ,
       \сумматор_9_out_4 , \сумматор_9_out_5 , \сумматор_10_out_4 , \сумматор_10_out_5 , \сумматор_11_out_5 ,
       \сумматор_12_out_5 ;
  wire [7:0] and_16_out;

  and and_1 (and_1_out, in_1[3], in_2[3]);
  \Сумматор  \u_сумматор_1  (
    .in_1(\сумматор_3_out_5 ), .in_2(and_1_out), .in_3(\сумматор_2_out_5 ), .out_5(and_16_out[7]),
    .out_4(and_16_out[6]));
  and and_2 (and_2_out, in_1[2], in_2[3]);
  \Сумматор  \u_сумматор_2  (
    .in_1(\сумматор_4_out_5 ), .in_2(and_3_out), .in_3(\сумматор_6_out_5 ), .out_5(\сумматор_2_out_5 ),
    .out_4(\сумматор_2_out_4 ));
  \Сумматор  \u_сумматор_3  (
    .in_1(\сумматор_5_out_5 ), .in_2(\сумматор_2_out_4 ), .in_3(and_2_out), .out_5(\сумматор_3_out_5 ),
    .out_4(and_16_out[5]));
  and and_3 (and_3_out, in_1[3], in_2[2]);
  and and_4 (and_4_out, in_1[1], in_2[3]);
  and and_5 (and_5_out, in_1[2], in_2[2]);
  \Сумматор  \u_сумматор_4  (
    .in_1(\сумматор_8_out_5 ), .in_2(\сумматор_6_out_4 ), .in_3(and_5_out), .out_5(\сумматор_4_out_5 ),
    .out_4(\сумматор_4_out_4 ));
  \Сумматор  \u_сумматор_5  (
    .in_1(\сумматор_7_out_5 ), .in_2(\сумматор_4_out_4 ), .in_3(and_4_out), .out_5(\сумматор_5_out_5 ),
    .out_4(and_16_out[4]));
  and and_6 (and_6_out, in_1[3], in_2[1]);
  \Сумматор  \u_сумматор_6  (
    .in_1(\сумматор_9_out_5 ), .in_2(and_6_out), .in_3(1'b0), .out_5(\сумматор_6_out_5 ),
    .out_4(\сумматор_6_out_4 ));
  and and_7 (and_7_out, in_1[1], in_2[2]);
  and and_8 (and_8_out, in_1[0], in_2[3]);
  \Сумматор  \u_сумматор_7  (
    .in_1(1'b0), .in_2(\сумматор_8_out_4 ), .in_3(and_8_out), .out_5(\сумматор_7_out_5 ),
    .out_4(and_16_out[3]));
  and and_9 (and_9_out, in_1[2], in_2[1]);
  \Сумматор  \u_сумматор_8  (
    .in_1(\сумматор_11_out_5 ), .in_2(\сумматор_9_out_4 ), .in_3(and_7_out), .out_5(\сумматор_8_out_5 ),
    .out_4(\сумматор_8_out_4 ));
  and and_10 (and_10_out, in_1[3], in_2[0]);
  \Сумматор  \u_сумматор_9  (
    .in_1(\сумматор_10_out_5 ), .in_2(and_10_out), .in_3(and_9_out), .out_5(\сумматор_9_out_5 ),
    .out_4(\сумматор_9_out_4 ));
  and and_11 (and_11_out, in_1[0], in_2[2]);
  and and_12 (and_12_out, in_1[1], in_2[1]);
  and and_13 (and_13_out, in_1[2], in_2[0]);
  \Сумматор  \u_сумматор_10  (
    .in_1(\сумматор_12_out_5 ), .in_2(and_13_out), .in_3(and_12_out), .out_5(\сумматор_10_out_5 ),
    .out_4(\сумматор_10_out_4 ));
  \Сумматор  \u_сумматор_11  (
    .in_1(1'b0), .in_2(\сумматор_10_out_4 ), .in_3(and_11_out), .out_5(\сумматор_11_out_5 ),
    .out_4(and_16_out[2]));
  and and_14 (and_14_out, in_1[0], in_2[1]);
  \Сумматор  \u_сумматор_12  (
    .in_1(1'b0), .in_2(and_15_out), .in_3(and_14_out), .out_5(\сумматор_12_out_5 ), .out_4(and_16_out[1]));
  and and_15 (and_15_out, in_1[1], in_2[0]);
  and and_16 (and_16_out[0], in_1[0], in_2[0]);
  // Probe on in_1
  // Probe on in_2
  // Probe on and_16_out
  // Probe on and_16_out
endmodule

module \Сдвигатель  (
  input  in_1,
  input  in_2,
  input  in_3,
  input  in_4,
  input  in_5,
  input  in_6,
  input  in_7,
  input  in_8,
  input  in_9,
  input  in_10,
  input  in_11,
  input  in_12,
  input  in_13,
  input  in_14,
  input  in_15,
  input  in_16,
  input  in_17,
  input  in_18,
  input  in_19,
  input  in_20,
  input  in_21,
  input  in_22,
  input  in_23,
  input  in_24,
  input  in_25,
  input  in_26,
  input  in_27,
  input  in_28,
  input  in_29,
  input  in_30,
  input  in_31,
  input  in_32,
  input  [7:0] in_33,
  input  [7:0] in_34,
  input  [7:0] in_35,
  input  [7:0] in_36,
  input  in_37,
  input  in_38,
  input  in_39,
  input  in_40,
  input  in_41,
  input  in_42,
  input  in_43,
  input  in_44,
  input  in_45,
  input  in_46,
  input  in_47,
  input  in_48,
  input  in_49,
  input  in_50,
  input  in_51,
  input  in_52,
  input  [7:0] in_53,
  input  [7:0] in_54,
  output out_55,
  output out_56,
  output out_57,
  output out_58,
  output out_59,
  output out_60,
  output out_61,
  output out_62,
  output out_63,
  output out_64,
  output out_65,
  output out_66,
  output out_67,
  output out_68,
  output out_69,
  output out_70,
  output out_71,
  output out_72,
  output out_73,
  output out_74,
  output out_75,
  output out_76,
  output out_77,
  output out_78,
  output out_79,
  output out_80,
  output out_81,
  output out_82,
  output out_83,
  output out_84,
  output out_85,
  output out_86,
  output [7:0] \Влево ,
  output [7:0] \Вправо ,
  output [7:0] \Влево_2 ,
  output [7:0] \Вправо_2 ,
  output out_91,
  output out_92,
  output out_93,
  output out_94,
  output out_95,
  output out_96,
  output out_97,
  output out_98,
  output out_99,
  output out_100,
  output out_101,
  output out_102,
  output out_103,
  output out_104,
  output out_105,
  output out_106,
  output [7:0] \Влево_3 ,
  output [7:0] \Вправо_3 
);

  // Probe on in_33
  // Probe on {in_33[6:0], 1'b0}
  // Probe on in_53
  // Probe on {in_53[6:0], in_53[7]}
  // Probe on in_34
  // Probe on {1'b0, in_34[7:1]}
  // Probe on {in_54[0], in_54[7:1]}
  // Probe on in_54
  // Probe on in_35
  // Probe on {in_35[7], in_35[5:0], 1'b0}
  // Probe on in_36
  // Probe on {{2{in_36[7]}}, in_36[6:1]}

  assign out_55 = in_2;
  assign out_56 = in_3;
  assign out_57 = in_4;
  assign out_58 = in_5;
  assign out_59 = in_6;
  assign out_60 = in_7;
  assign out_61 = in_8;
  assign out_62 = 1'b0;
  assign out_63 = 1'b0;
  assign out_64 = in_9;
  assign out_65 = in_10;
  assign out_66 = in_11;
  assign out_67 = in_12;
  assign out_68 = in_13;
  assign out_69 = in_14;
  assign out_70 = in_15;
  assign out_71 = in_17;
  assign out_72 = in_19;
  assign out_73 = in_20;
  assign out_74 = in_21;
  assign out_75 = in_22;
  assign out_76 = in_23;
  assign out_77 = in_24;
  assign out_78 = 1'b0;
  assign out_79 = in_25;
  assign out_80 = in_25;
  assign out_81 = in_26;
  assign out_82 = in_27;
  assign out_83 = in_28;
  assign out_84 = in_29;
  assign out_85 = in_30;
  assign out_86 = in_31;
  assign out_91 = in_38;
  assign out_92 = in_39;
  assign out_93 = in_40;
  assign out_94 = in_41;
  assign out_95 = in_42;
  assign out_96 = in_43;
  assign out_97 = in_44;
  assign out_98 = in_37;
  assign out_99 = in_52;
  assign out_100 = in_45;
  assign out_101 = in_46;
  assign out_102 = in_47;
  assign out_103 = in_48;
  assign out_104 = in_49;
  assign out_105 = in_50;
  assign out_106 = in_51;
  assign \Влево  = {in_33[6:0], 1'b0};
  assign \Влево_2  = {in_35[7], in_35[5:0], 1'b0};
  assign \Влево_3  = {in_53[6:0], in_53[7]};
  assign \Вправо  = {1'b0, in_34[7:1]};
  assign \Вправо_2  = {{2{in_36[7]}}, in_36[6:1]};
  assign \Вправо_3  = {in_54[0], in_54[7:1]};

  // Notes on the sheet:
  //   Логический сдвиг
  //   Циклический сдвиг
  //   Арифметический сдвиг
endmodule
