// Logisim project Lab_3_Shifrator.circ as structural Verilog: 11 circuits, main circuit От 0 до 9
module \От_0_до_9  (
  input  X0,
  input  X1,
  input  X2,
  input  X3,
  input  X4,
  input  X5,
  input  X6,
  input  X7,
  input  X8,
  input  X9,
  output out_11,
  output out_12,
  output out_13,
  output out_14
);

  wire and_1_out, and_2_out, and_3_out, and_4_out, and_5_out, and_6_out, and_7_out, and_8_out, and_9_out,
       and_10_out, and_11_out, and_12_out, and_13_out, and_14_out, and_15_out, and_16_out, and_17_out,
       and_18_out, not_1_out, not_2_out, not_3_out, not_4_out, not_5_out, not_6_out, not_7_out, not_8_out,
       not_9_out, not_10_out, not_11_out, not_12_out, not_13_out, not_14_out, not_15_out, not_16_out,
       not_17_out, not_18_out, not_19_out, not_20_out, not_21_out, not_22_out, not_23_out, not_24_out,
       not_25_out, not_26_out, not_27_out, not_28_out, not_29_out, not_30_out, not_31_out, not_32_out,
       not_33_out, not_34_out, not_35_out, not_36_out, not_37_out, not_38_out, not_39_out, not_40_out,
       not_41_out, not_42_out, not_43_out, not_44_out, not_45_out, not_46_out, not_47_out, not_48_out,
       not_49_out, not_50_out, not_51_out, not_52_out, not_53_out, not_54_out, not_55_out, not_56_out,
       not_57_out, not_58_out, not_59_out, not_60_out, not_61_out, not_62_out, not_63_out, not_64_out,
       not_65_out, not_66_out, not_67_out, not_68_out, not_69_out, not_70_out, not_71_out, not_72_out,
       not_73_out, not_74_out, not_75_out, not_76_out, not_77_out, not_78_out, not_79_out, not_80_out,
       not_81_out, not_82_out, not_83_out, not_84_out, not_85_out, not_86_out, not_87_out, not_88_out,
       not_89_out, not_90_out, not_91_out, not_92_out, not_93_out, not_94_out, not_95_out, not_96_out,
       not_97_out, not_98_out, not_99_out, not_100_out, not_101_out, not_102_out, not_103_out, not_104_out,
       not_105_out, not_106_out, not_107_out, not_108_out, not_109_out, not_110_out, not_111_out,
       not_112_out, not_113_out, not_114_out, not_115_out, not_116_out, not_117_out, not_118_out,
       not_119_out, not_120_out, not_121_out, not_122_out, not_123_out, not_124_out, not_125_out,
       not_126_out, not_127_out, not_128_out, not_129_out, not_130_out, not_131_out, not_132_out,
       not_133_out, not_134_out, not_135_out, not_136_out, not_137_out, not_138_out, not_139_out,
       not_140_out, not_141_out, not_142_out, not_143_out, not_144_out, not_145_out, not_146_out,
       not_147_out, not_148_out, not_149_out, not_150_out, not_151_out, not_152_out, not_153_out, not_154_out;

  not not_1 (not_1_out, X9);
  not not_2 (not_2_out, X7);
  not not_3 (not_3_out, X6);
  not not_4 (not_4_out, X5);
  not not_5 (not_5_out, X4);
  not not_6 (not_6_out, X3);
  not not_7 (not_7_out, X2);
  not not_8 (not_8_out, X1);
  not not_9 (not_9_out, X0);
  not not_10 (not_10_out, X9);
  not not_11 (not_11_out, X7);
  not not_12 (not_12_out, X6);
  not not_13 (not_13_out, X5);
  not not_14 (not_14_out, X4);
  not not_15 (not_15_out, X3);
  not not_16 (not_16_out, X2);
  not not_17 (not_17_out, X1);
  not not_18 (not_18_out, X0);
  not not_19 (not_19_out, X8);
  not not_20 (not_20_out, X7);
  not not_21 (not_21_out, X6);
  not not_22 (not_22_out, X5);
  not not_23 (not_23_out, X4);
  not not_24 (not_24_out, X3);
  not not_25 (not_25_out, X2);
  not not_26 (not_26_out, X1);
  not not_27 (not_27_out, X0);
  not not_28 (not_28_out, X9);
  not not_29 (not_29_out, X8);
  not not_30 (not_30_out, X7);
  not not_31 (not_31_out, X6);
  not not_32 (not_32_out, X5);
  not not_33 (not_33_out, X3);
  not not_34 (not_34_out, X2);
  not not_35 (not_35_out, X1);
  not not_36 (not_36_out, X0);
  not not_37 (not_37_out, X9);
  not not_38 (not_38_out, X8);
  not not_39 (not_39_out, X7);
  not not_40 (not_40_out, X6);
  not not_41 (not_41_out, X4);
  not not_42 (not_42_out, X3);
  not not_43 (not_43_out, X2);
  not not_44 (not_44_out, X1);
  not not_45 (not_45_out, X0);
  not not_46 (not_46_out, X9);
  not not_47 (not_47_out, X8);
  not not_48 (not_48_out, X7);
  not not_49 (not_49_out, X5);
  not not_50 (not_50_out, X4);
  not not_51 (not_51_out, X3);
  not not_52 (not_52_out, X2);
  not not_53 (not_53_out, X1);
  not not_54 (not_54_out, X0);
  not not_55 (not_55_out, X9);
  not not_56 (not_56_out, X8);
  not not_57 (not_57_out, X6);
  not not_58 (not_58_out, X5);
  not not_59 (not_59_out, X4);
  not not_60 (not_60_out, X3);
  not not_61 (not_61_out, X2);
  not not_62 (not_62_out, X1);
  not not_63 (not_63_out, X0);
  not not_64 (not_64_out, X9);
  not not_65 (not_65_out, X8);
  not not_66 (not_66_out, X7);
  not not_67 (not_67_out, X6);
  not not_68 (not_68_out, X5);
  not not_69 (not_69_out, X4);
  not not_70 (not_70_out, X3);
  not not_71 (not_71_out, X1);
  not not_72 (not_72_out, X0);
  not not_73 (not_73_out, X9);
  not not_74 (not_74_out, X8);
  not not_75 (not_75_out, X7);
  not not_76 (not_76_out, X6);
  not not_77 (not_77_out, X5);
  not not_78 (not_78_out, X4);
  not not_79 (not_79_out, X2);
  not not_80 (not_80_out, X1);
  not not_81 (not_81_out, X0);
  not not_82 (not_82_out, X9);
  not not_83 (not_83_out, X8);
  not not_84 (not_84_out, X7);
  not not_85 (not_85_out, X5);
  not not_86 (not_86_out, X4);
  not not_87 (not_87_out, X3);
  not not_88 (not_88_out, X2);
  not not_89 (not_89_out, X1);
  not not_90 (not_90_out, X0);
  not not_91 (not_91_out, X9);
  not not_92 (not_92_out, X8);
  not not_93 (not_93_out, X6);
  not not_94 (not_94_out, X5);
  not not_95 (not_95_out, X4);
  not not_96 (not_96_out, X3);
  not not_97 (not_97_out, X2);
  not not_98 (not_98_out, X1);
  not not_99 (not_99_out, X0);
  not not_100 (not_100_out, X9);
  not not_101 (not_101_out, X7);
  not not_102 (not_102_out, X4);
  not not_103 (not_103_out, X3);
  not not_104 (not_104_out, X1);
  not not_105 (not_105_out, X0);
  not not_106 (not_106_out, X9);
  not not_107 (not_107_out, X8);
  not not_108 (not_108_out, X7);
  not not_109 (not_109_out, X6);
  not not_110 (not_110_out, X4);
  not not_111 (not_111_out, X3);
  not not_112 (not_112_out, X2);
  not not_113 (not_113_out, X0);
  not not_114 (not_114_out, X9);
  not not_115 (not_115_out, X8);
  not not_116 (not_116_out, X7);
  not not_117 (not_117_out, X6);
  not not_118 (not_118_out, X5);
  not not_119 (not_119_out, X4);
  not not_120 (not_120_out, X2);
  not not_121 (not_121_out, X1);
  not not_122 (not_122_out, X0);
  not not_123 (not_123_out, X9);
  not not_124 (not_124_out, X8);
  not not_125 (not_125_out, X7);
  not not_126 (not_126_out, X6);
  not not_127 (not_127_out, X4);
  not not_128 (not_128_out, X3);
  not not_129 (not_129_out, X2);
  not not_130 (not_130_out, X0);
  not not_131 (not_131_out, X9);
  not not_132 (not_132_out, X8);
  not not_133 (not_133_out, X6);
  not not_134 (not_134_out, X5);
  not not_135 (not_135_out, X4);
  not not_136 (not_136_out, X3);
  not not_137 (not_137_out, X2);
  not not_138 (not_138_out, X1);
  not not_139 (not_139_out, X0);
  not not_140 (not_140_out, X9);
  not not_141 (not_141_out, X7);
  not not_142 (not_142_out, X6);
  not not_143 (not_143_out, X3);
  not not_144 (not_144_out, X2);
  not not_145 (not_145_out, X0);
  not not_146 (not_146_out, X8);
  not not_147 (not_147_out, X7);
  not not_148 (not_148_out, X6);
  not not_149 (not_149_out, X5);
  not not_150 (not_150_out, X4);
  not not_151 (not_151_out, X3);
  not not_152 (not_152_out, X2);
  not not_153 (not_153_out, X1);
  not not_154 (not_154_out, X0);
  and and_1 (and_1_out, not_1_out, X8, not_2_out, not_3_out, not_4_out, not_5_out, not_6_out, not_7_out, not_8_out, not_9_out);
  and and_2 (and_2_out, not_10_out, X8, not_11_out, not_12_out, not_13_out, not_14_out, not_15_out, not_16_out, not_17_out, not_18_out);
  and and_3 (and_3_out, X9, not_19_out, not_20_out, not_21_out, not_22_out, not_23_out, not_24_out, not_25_out, not_26_out, not_27_out);
  and and_4 (and_4_out, not_28_out, not_29_out, not_30_out, not_31_out, not_32_out, X4, not_33_out, not_34_out, not_35_out, not_36_out);
  and and_5 (and_5_out, not_37_out, not_38_out, not_39_out, not_40_out, X5, not_41_out, not_42_out, not_43_out, not_44_out, not_45_out);
  and and_6 (and_6_out, not_46_out, not_47_out, not_48_out, X6, not_49_out, not_50_out, not_51_out, not_52_out, not_53_out, not_54_out);
  and and_7 (and_7_out, not_55_out, not_56_out, X7, not_57_out, not_58_out, not_59_out, not_60_out, not_61_out, not_62_out, not_63_out);
  and and_8 (and_8_out, not_64_out, not_65_out, not_66_out, not_67_out, not_68_out, not_69_out, not_70_out, X2, not_71_out, not_72_out);
  and and_9 (and_9_out, not_73_out, not_74_out, not_75_out, not_76_out, not_77_out, not_78_out, X3, not_79_out, not_80_out, not_81_out);
  and and_10 (and_10_out, not_82_out, not_83_out, not_84_out, X6, not_85_out, not_86_out, not_87_out, not_88_out, not_89_out, not_90_out);
  and and_11 (and_11_out, not_91_out, not_92_out, X7, not_93_out, not_94_out, not_95_out, not_96_out, not_97_out, not_98_out, not_99_out);
  and and_12 (and_12_out, not_100_out, X8, not_101_out, X6, X5, not_102_out, not_103_out, X2, not_104_out, not_105_out);
  and and_13 (and_13_out, not_106_out, not_107_out, not_108_out, not_109_out, not_110_out, not_111_out, not_112_out, X1, not_113_out);
  and and_14 (and_14_out, not_114_out, not_115_out, not_116_out, not_117_out, not_118_out, not_119_out, X3, not_120_out, not_121_out, not_122_out);
  and and_15 (and_15_out, not_123_out, not_124_out, not_125_out, not_126_out, X5, not_127_out, not_128_out, not_129_out, not_130_out);
  and and_16 (and_16_out, not_131_out, not_132_out, X7, not_133_out, not_134_out, not_135_out, not_136_out, not_137_out, not_138_out, not_139_out);
  and and_17 (and_17_out, not_140_out, X8, not_141_out, not_142_out, X5, X4, not_143_out, not_144_out, X1, not_145_out);
  and and_18 (and_18_out, X9, not_146_out, not_147_out, not_148_out, not_149_out, not_150_out, not_151_out, not_152_out, not_153_out, not_154_out);
  or or_1 (out_11, and_1_out, and_2_out, and_3_out);
  or or_2 (out_12, and_4_out, and_5_out, and_6_out, and_7_out);
  or or_3 (out_13, and_8_out, and_9_out, and_10_out, and_11_out, and_12_out);
  or or_4 (out_14, and_13_out, and_14_out, and_15_out, and_16_out, and_17_out, and_18_out);
endmodule

module \Шифратор_от_A_до_F  (
  input  A,
  input  B,
  input  C,
  input  D,
  input  E,
  input  F,
  output G3,
  output G2,
  output G1,
  output G0
);

  wire and_1_out, and_2_out, and_3_out, and_4_out, and_5_out, and_6_out, and_7_out, and_8_out, and_9_out,
       and_10_out, and_11_out, and_12_out, and_13_out, and_14_out, and_15_out, and_16_out, and_17_out,
       not_1_out, not_2_out, not_3_out, not_4_out, not_5_out, not_6_out, not_7_out, not_8_out, not_9_out,
       not_10_out, not_11_out, not_12_out, not_13_out, not_14_out, not_15_out, not_16_out, not_17_out,
       not_18_out, not_19_out, not_20_out, not_21_out, not_22_out, not_23_out, not_24_out, not_25_out,
       not_26_out, not_27_out, not_28_out, not_29_out, not_30_out, not_31_out, not_32_out, not_33_out,
       not_34_out, not_35_out, not_36_out, not_37_out, not_38_out, not_39_out, not_40_out, not_41_out,
       not_42_out, not_43_out, not_44_out, not_45_out, not_46_out, not_47_out, not_48_out, not_49_out,
       not_50_out, not_51_out, not_52_out, not_53_out, not_54_out, not_55_out, not_56_out, not_57_out,
       not_58_out, not_59_out, not_60_out, not_61_out, not_62_out, not_63_out, not_64_out, not_65_out,
       not_66_out, not_67_out, not_68_out, not_69_out, not_70_out, not_71_out, not_72_out, not_73_out,
       not_74_out, not_75_out, not_76_out, not_77_out, not_78_out, not_79_out, not_80_out, not_81_out,
       not_82_out, not_83_out, not_84_out, not_85_out;

  not not_1 (not_1_out, A);
  not not_2 (not_2_out, C);
  not not_3 (not_3_out, D);
  not not_4 (not_4_out, E);
  not not_5 (not_5_out, F);
  not not_6 (not_6_out, A);
  not not_7 (not_7_out, B);
  not not_8 (not_8_out, C);
  not not_9 (not_9_out, E);
  not not_10 (not_10_out, F);
  not not_11 (not_11_out, A);
  not not_12 (not_12_out, B);
  not not_13 (not_13_out, C);
  not not_14 (not_14_out, D);
  not not_15 (not_15_out, E);
  not not_16 (not_16_out, B);
  not not_17 (not_17_out, C);
  not not_18 (not_18_out, D);
  not not_19 (not_19_out, E);
  not not_20 (not_20_out, F);
  not not_21 (not_21_out, A);
  not not_22 (not_22_out, C);
  not not_23 (not_23_out, D);
  not not_24 (not_24_out, E);
  not not_25 (not_25_out, F);
  not not_26 (not_26_out, A);
  not not_27 (not_27_out, B);
  not not_28 (not_28_out, C);
  not not_29 (not_29_out, D);
  not not_30 (not_30_out, F);
  not not_31 (not_31_out, A);
  not not_32 (not_32_out, B);
  not not_33 (not_33_out, C);
  not not_34 (not_34_out, D);
  not not_35 (not_35_out, E);
  not not_36 (not_36_out, A);
  not not_37 (not_37_out, B);
  not not_38 (not_38_out, D);
  not not_39 (not_39_out, E);
  not not_40 (not_40_out, F);
  not not_41 (not_41_out, A);
  not not_42 (not_42_out, B);
  not not_43 (not_43_out, C);
  not not_44 (not_44_out, E);
  not not_45 (not_45_out, F);
  not not_46 (not_46_out, A);
  not not_47 (not_47_out, B);
  not not_48 (not_48_out, C);
  not not_49 (not_49_out, D);
  not not_50 (not_50_out, F);
  not not_51 (not_51_out, A);
  not not_52 (not_52_out, B);
  not not_53 (not_53_out, C);
  not not_54 (not_54_out, D);
  not not_55 (not_55_out, E);
  not not_56 (not_56_out, B);
  not not_57 (not_57_out, C);
  not not_58 (not_58_out, D);
  not not_59 (not_59_out, E);
  not not_60 (not_60_out, F);
  not not_61 (not_61_out, A);
  not not_62 (not_62_out, C);
  not not_63 (not_63_out, D);
  not not_64 (not_64_out, E);
  not not_65 (not_65_out, F);
  not not_66 (not_66_out, A);
  not not_67 (not_67_out, B);
  not not_68 (not_68_out, D);
  not not_69 (not_69_out, E);
  not not_70 (not_70_out, F);
  not not_71 (not_71_out, A);
  not not_72 (not_72_out, B);
  not not_73 (not_73_out, C);
  not not_74 (not_74_out, E);
  not not_75 (not_75_out, F);
  not not_76 (not_76_out, A);
  not not_77 (not_77_out, B);
  not not_78 (not_78_out, C);
  not not_79 (not_79_out, D);
  not not_80 (not_80_out, F);
  not not_81 (not_81_out, A);
  not not_82 (not_82_out, B);
  not not_83 (not_83_out, C);
  not not_84 (not_84_out, D);
  not not_85 (not_85_out, E);
  and and_1 (and_1_out, not_1_out, B, not_2_out, not_3_out, not_4_out, not_5_out);
  and and_2 (and_2_out, not_6_out, not_7_out, not_8_out, D, not_9_out, not_10_out);
  and and_3 (and_3_out, not_11_out, not_12_out, not_13_out, not_14_out, not_15_out, F);
  and and_4 (and_4_out, A, not_16_out, not_17_out, not_18_out, not_19_out, not_20_out);
  and and_5 (and_5_out, not_21_out, B, not_22_out, not_23_out, not_24_out, not_25_out);
  and and_6 (and_6_out, not_26_out, not_27_out, not_28_out, not_29_out, E, not_30_out);
  and and_7 (and_7_out, not_31_out, not_32_out, not_33_out, not_34_out, not_35_out, F);
  and and_8 (and_8_out, not_36_out, not_37_out, C, not_38_out, not_39_out, not_40_out);
  and and_9 (and_9_out, not_41_out, not_42_out, not_43_out, D, not_44_out, not_45_out);
  and and_10 (and_10_out, not_46_out, not_47_out, not_48_out, not_49_out, E, not_50_out);
  and and_11 (and_11_out, not_51_out, not_52_out, not_53_out, not_54_out, not_55_out, F);
  and and_12 (and_12_out, A, not_56_out, not_57_out, not_58_out, not_59_out, not_60_out);
  and and_13 (and_13_out, not_61_out, B, not_62_out, not_63_out, not_64_out, not_65_out);
  and and_14 (and_14_out, not_66_out, not_67_out, C, not_68_out, not_69_out, not_70_out);
  and and_15 (and_15_out, not_71_out, not_72_out, not_73_out, D, not_74_out, not_75_out);
  and and_16 (and_16_out, not_76_out, not_77_out, not_78_out, not_79_out, E, not_80_out);
  and and_17 (and_17_out, not_81_out, not_82_out, not_83_out, not_84_out, not_85_out, F);
  or or_1 (G0, and_1_out, and_2_out, and_3_out);
  or or_2 (G1, and_4_out, and_5_out, and_6_out, and_7_out);
  or or_3 (G2, and_8_out, and_9_out, and_10_out, and_11_out);
  or or_4 (G3, and_12_out, and_13_out, and_14_out, and_15_out, and_16_out, and_17_out);
endmodule

module \Разделение_шифраторов  (
  input  X3,
  input  X2,
  input  X1,
  input  X0,
  input  Y3,
  input  Y2,
  input  Y1,
  input  Y0,
  output Z3,
  output Z2,
  output Z1,
  output Z0
);

  wire and_1_out, and_2_out, and_3_out, and_4_out, and_5_out, and_6_out, and_7_out, and_8_out, not_1_out,
       not_2_out, not_3_out, not_4_out, not_5_out, not_6_out, not_7_out, not_8_out, not_9_out, not_10_out,
       not_11_out, not_12_out, not_13_out, not_14_out, not_15_out, not_16_out, not_17_out, not_18_out,
       not_19_out, not_20_out, not_21_out, not_22_out, not_23_out, not_24_out, not_25_out, not_26_out,
       not_27_out, not_28_out, not_29_out, not_30_out, not_31_out, not_32_out;

  not not_1 (not_1_out, X3);
  not not_2 (not_2_out, X2);
  not not_3 (not_3_out, X1);
  not not_4 (not_4_out, X0);
  not not_5 (not_5_out, Y3);
  not not_6 (not_6_out, Y2);
  not not_7 (not_7_out, Y1);
  not not_8 (not_8_out, Y0);
  not not_9 (not_9_out, X3);
  not not_10 (not_10_out, X2);
  not not_11 (not_11_out, X1);
  not not_12 (not_12_out, X0);
  not not_13 (not_13_out, Y3);
  not not_14 (not_14_out, Y2);
  not not_15 (not_15_out, Y1);
  not not_16 (not_16_out, Y0);
  not not_17 (not_17_out, X3);
  not not_18 (not_18_out, X2);
  not not_19 (not_19_out, X1);
  not not_20 (not_20_out, X0);
  not not_21 (not_21_out, Y3);
  not not_22 (not_22_out, Y2);
  not not_23 (not_23_out, Y1);
  not not_24 (not_24_out, Y0);
  not not_25 (not_25_out, X3);
  not not_26 (not_26_out, X2);
  not not_27 (not_27_out, X1);
  not not_28 (not_28_out, X0);
  not not_29 (not_29_out, Y3);
  not not_30 (not_30_out, Y2);
  not not_31 (not_31_out, Y1);
  not not_32 (not_32_out, Y0);
  and and_1 (and_1_out, not_1_out, not_2_out, not_3_out, not_4_out, Y3);
  or or_1 (Z3, and_1_out, and_2_out);
  and and_2 (and_2_out, X3, not_5_out, not_6_out, not_7_out, not_8_out);
  and and_3 (and_3_out, not_9_out, not_10_out, not_11_out, not_12_out, Y2);
  or or_2 (Z2, and_3_out, and_4_out);
  and and_4 (and_4_out, X2, not_13_out, not_14_out, not_15_out, not_16_out);
  and and_5 (and_5_out, not_17_out, not_18_out, not_19_out, not_20_out, Y1);
  or or_3 (Z1, and_5_out, and_6_out);
  and and_6 (and_6_out, X1, not_21_out, not_22_out, not_23_out, not_24_out);
  and and_7 (and_7_out, not_25_out, not_26_out, not_27_out, not_28_out, Y0);
  or or_4 (Z0, and_7_out, and_8_out);
  and and_8 (and_8_out, X0, not_29_out, not_30_out, not_31_out, not_32_out);
endmodule

module \Шифратор_из_16_в_2  (
  input  in_1,
  input  in_2,
  input  in_3,
  input  in_4,
  input  in_5,
  input  in_6,
  input  in_7,
  input  in_8,
  input  in_9,
  input  in_10,
  input  in_11,
  input  in_12,
  input  in_13,
  input  in_14,
  input  in_15,
  input  in_16,
  output [3:0] out_17
);

  wire \от_0_до_9_1_out_11 , \от_0_до_9_1_out_12 , \от_0_до_9_1_out_13 , \от_0_до_9_1_out_14 ,
       \шифратор_от_a_до_f_1_g0 , \шифратор_от_a_до_f_1_g1 , \шифратор_от_a_до_f_1_g2 ,
       \шифратор_от_a_до_f_1_g3 ;

  \От_0_до_9  \u_от_0_до_9_1  (
    .X0(in_1), .X1(in_2), .X2(in_3), .X3(in_4), .X4(in_5), .X5(in_6), .X6(in_7), .X7(in_8), .X8(in_9),
    .X9(in_10), .out_11(\от_0_до_9_1_out_11 ), .out_12(\от_0_до_9_1_out_12 ), .out_13(\от_0_до_9_1_out_13 ),
    .out_14(\от_0_до_9_1_out_14 ));
  \Шифратор_от_A_до_F  \u_шифратор_от_a_до_f_1  (
    .A(in_11), .B(in_12), .C(in_13), .D(in_14), .E(in_15), .F(in_16), .G3(\шифратор_от_a_до_f_1_g3 ),
    .G2(\шифратор_от_a_до_f_1_g2 ), .G1(\шифратор_от_a_до_f_1_g1 ), .G0(\шифратор_от_a_до_f_1_g0 ));
  \Разделение_шифраторов  \u_разделение_шифраторов_1  (
    .X3(\от_0_до_9_1_out_11 ), .X2(\от_0_до_9_1_out_12 ), .X1(\от_0_до_9_1_out_13 ),
    .X0(\от_0_до_9_1_out_14 ), .Y3(\шифратор_от_a_до_f_1_g3 ), .Y2(\шифратор_от_a_до_f_1_g2 ),
    .Y1(\шифратор_от_a_до_f_1_g1 ), .Y0(\шифратор_от_a_до_f_1_g0 ), .Z3(out_17[3]), .Z2(out_17[2]),
    .Z1(out_17[1]), .Z0(out_17[0]));
  // Probe on out_17
endmodule

module \Дешифрaтор  (
  input  in_1,
  input  in_2,
  input  in_3,
  input  in_4,
  output _0,
  output _1,
  output _2,
  output _3,
  output _4,
  output _5,
  output _6,
  output _7,
  output _8,
  output _9,
  output A,
  output B,
  output C,
  output D,
  output E,
  output F
);

  and and_1 (_0, ~in_1, ~in_2, ~in_3, ~in_4);  // AND_Gate
  and and_2 (_1, ~in_1, ~in_2, ~in_3, in_4);  // AND_Gate
  and and_3 (_2, ~in_1, ~in_2, in_3, ~in_4);  // AND_Gate
  and and_4 (_3, ~in_1, ~in_2, in_3, in_4);  // AND_Gate
  and and_5 (_4, ~in_1, in_2, ~in_3, ~in_4);  // AND_Gate
  and and_6 (_5, ~in_1, in_2, ~in_3, in_4);  // AND_Gate
  and and_7 (_6, ~in_1, in_2, in_3, ~in_4);  // AND_Gate
  and and_8 (_7, ~in_1, in_2, in_3, in_4);  // AND_Gate
  and and_9 (_8, in_1, ~in_2, ~in_3, ~in_4);  // AND_Gate
  and and_10 (_9, in_1, ~in_2, ~in_3, in_4);  // AND_Gate
  and and_11 (A, in_1, ~in_2, in_3, ~in_4);  // AND_Gate
  and and_12 (B, in_1, ~in_2, in_3, in_4);  // AND_Gate
  and and_13 (C, in_1, in_2, ~in_3, ~in_4);  // AND_Gate
  and and_14 (D, in_1, in_2, ~in_3, in_4);  // AND_Gate
  and and_15 (E, in_1, in_2, in_3, ~in_4);  // AND_Gate
  and and_16 (F, in_1, in_2, in_3, in_4);
endmodule

module \Индикатор  (
  input  in_1,
  input  in_2,
  input  in_3,
  input  in_4,
  output out_5,
  output out_6,
  output out_7,
  output out_8,
  output out_9,
  output out_10,
  output out_11
);

  wire \дешифрaтор_1__0 , \дешифрaтор_1__1 , \дешифрaтор_1__2 , \дешифрaтор_1__3 , \дешифрaтор_1__4 ,
       \дешифрaтор_1__5 , \дешифрaтор_1__6 , \дешифрaтор_1__7 , \дешифрaтор_1__8 , \дешифрaтор_1__9 ,
       \дешифрaтор_1_a , \дешифрaтор_1_b , \дешифрaтор_1_c , \дешифрaтор_1_d , \дешифрaтор_1_e ,
       \дешифрaтор_1_f ;

  \Дешифрaтор  \u_дешифрaтор_1  (
    .in_1(in_1), .in_2(in_2), .in_3(in_3), .in_4(in_4), ._0(\дешифрaтор_1__0 ), ._1(\дешифрaтор_1__1 ),
    ._2(\дешифрaтор_1__2 ), ._3(\дешифрaтор_1__3 ), ._4(\дешифрaтор_1__4 ), ._5(\дешифрaтор_1__5 ),
    ._6(\дешифрaтор_1__6 ), ._7(\дешифрaтор_1__7 ), ._8(\дешифрaтор_1__8 ), ._9(\дешифрaтор_1__9 ),
    .A(\дешифрaтор_1_a ), .B(\дешифрaтор_1_b ), .C(\дешифрaтор_1_c ), .D(\дешифрaтор_1_d ),
    .E(\дешифрaтор_1_e ), .F(\дешифрaтор_1_f ));
  or or_1 (out_5, \дешифрaтор_1_f , \дешифрaтор_1_e , \дешифрaтор_1_d , \дешифрaтор_1_b , \дешифрaтор_1_a , \дешифрaтор_1__9 , \дешифрaтор_1__8 , \дешифрaтор_1__6 , \дешифрaтор_1__5 , \дешифрaтор_1__4 , \дешифрaтор_1__3 , \дешифрaтор_1__2 );
  or or_2 (out_6, \дешифрaтор_1_f , \дешифрaтор_1_e , \дешифрaтор_1_c , \дешифрaтор_1_b , \дешифрaтор_1_a , \дешифрaтор_1__9 , \дешифрaтор_1__8 , \дешифрaтор_1__6 , \дешифрaтор_1__5 , \дешифрaтор_1__4 , \дешифрaтор_1__0 );
  or or_3 (out_7, \дешифрaтор_1_f , \дешифрaтор_1_e , \дешифрaтор_1_c , \дешифрaтор_1_a , \дешифрaтор_1__9 , \дешифрaтор_1__8 , \дешифрaтор_1__7 , \дешифрaтор_1__6 , \дешифрaтор_1__5 , \дешифрaтор_1__3 , \дешифрaтор_1__2 , \дешифрaтор_1__0 );
  or or_4 (out_8, \дешифрaтор_1_d , \дешифрaтор_1_a , \дешифрaтор_1__9 , \дешифрaтор_1__8 , \дешифрaтор_1__7 , \дешифрaтор_1__4 , \дешифрaтор_1__3 , \дешифрaтор_1__2 , \дешифрaтор_1__1 , \дешифрaтор_1__0 );
  or or_5 (out_9, \дешифрaтор_1_f , \дешифрaтор_1_e , \дешифрaтор_1_d , \дешифрaтор_1_c , \дешифрaтор_1_b , \дешифрaтор_1_a , \дешифрaтор_1__8 , \дешифрaтор_1__6 , \дешифрaтор_1__2 , \дешифрaтор_1__0 );
  or or_6 (out_10, \дешифрaтор_1_e , \дешифрaтор_1_d , \дешифрaтор_1_c , \дешифрaтор_1_b , \дешифрaтор_1__9 , \дешифрaтор_1__8 , \дешифрaтор_1__6 , \дешифрaтор_1__5 , \дешифрaтор_1__3 , \дешифрaтор_1__2 , \дешифрaтор_1__0 );
  or or_7 (out_11, \дешифрaтор_1_d , \дешифрaтор_1_b , \дешифрaтор_1_a , \дешифрaтор_1__9 , \дешифрaтор_1__8 , \дешифрaтор_1__7 , \дешифрaтор_1__6 , \дешифрaтор_1__5 , \дешифрaтор_1__4 , \дешифрaтор_1__3 , \дешифрaтор_1__1 , \дешифрaтор_1__0 );
endmodule

module \Шестнадцатеричный_шифратор_с_индикатором  (
  input  in_1,
  input  in_2,
  input  in_3,
  input  in_4,
  input  in_5,
  input  in_6,
  input  in_7,
  input  in_8,
  input  in_9,
  input  in_10,
  input  in_11,
  input  in_12,
  input  in_13,
  input  in_14,
  input  in_15,
  input  in_16
);

  wire \индикатор_1_out_5 , \индикатор_1_out_6 , \индикатор_1_out_7 , \индикатор_1_out_8 ,
       \индикатор_1_out_9 , \индикатор_1_out_10 , \индикатор_1_out_11 , \от_0_до_9_1_out_11 ,
       \от_0_до_9_1_out_12 , \от_0_до_9_1_out_13 , \от_0_до_9_1_out_14 , \разделение_шифраторов_1_z0 ,
       \разделение_шифраторов_1_z1 , \разделение_шифраторов_1_z2 , \разделение_шифраторов_1_z3 ,
       \шифратор_от_a_до_f_1_g0 , \шифратор_от_a_до_f_1_g1 , \шифратор_от_a_до_f_1_g2 ,
       \шифратор_от_a_до_f_1_g3 ;

  \От_0_до_9  \u_от_0_до_9_1  (
    .X0(in_1), .X1(in_2), .X2(in_3), .X3(in_4), .X4(in_5), .X5(in_6), .X6(in_7), .X7(in_8), .X8(in_9),
    .X9(in_10), .out_11(\от_0_до_9_1_out_11 ), .out_12(\от_0_до_9_1_out_12 ), .out_13(\от_0_до_9_1_out_13 ),
    .out_14(\от_0_до_9_1_out_14 ));
  \Шифратор_от_A_до_F  \u_шифратор_от_a_до_f_1  (
    .A(in_11), .B(in_12), .C(in_13), .D(in_14), .E(in_15), .F(in_16), .G3(\шифратор_от_a_до_f_1_g3 ),
    .G2(\шифратор_от_a_до_f_1_g2 ), .G1(\шифратор_от_a_до_f_1_g1 ), .G0(\шифратор_от_a_до_f_1_g0 ));
  \Разделение_шифраторов  \u_разделение_шифраторов_1  (
    .X3(\от_0_до_9_1_out_11 ), .X2(\от_0_до_9_1_out_12 ), .X1(\от_0_до_9_1_out_13 ),
    .X0(\от_0_до_9_1_out_14 ), .Y3(\шифратор_от_a_до_f_1_g3 ), .Y2(\шифратор_от_a_до_f_1_g2 ),
    .Y1(\шифратор_от_a_до_f_1_g1 ), .Y0(\шифратор_от_a_до_f_1_g0 ), .Z3(\разделение_шифраторов_1_z3 ),
    .Z2(\разделение_шифраторов_1_z2 ), .Z1(\разделение_шифраторов_1_z1 ), .Z0(\разделение_шифраторов_1_z0 ));
  \Индикатор  \u_индикатор_1  (
    .in_1(\разделение_шифраторов_1_z3 ), .in_2(\разделение_шифраторов_1_z2 ),
    .in_3(\разделение_шифраторов_1_z1 ), .in_4(\разделение_шифраторов_1_z0 ), .out_5(\индикатор_1_out_5 ),
    .out_6(\индикатор_1_out_6 ), .out_7(\индикатор_1_out_7 ), .out_8(\индикатор_1_out_8 ),
    .out_9(\индикатор_1_out_9 ), .out_10(\индикатор_1_out_10 ), .out_11(\индикатор_1_out_11 ));
  _7_Segment_Display u_7_segment_display_1 (
    .g(\индикатор_1_out_5 ), .f(\индикатор_1_out_6 ), .a(\индикатор_1_out_7 ), .b(\индикатор_1_out_8 ),
    .e(\индикатор_1_out_9 ), .d(\индикатор_1_out_10 ), .c(\индикатор_1_out_11 ), .dp(1'b0));
endmodule

module \Мультиплексор  (
  input  X0,
  input  X1,
  input  X2,
  input  X3,
  input  X4,
  input  X5,
  input  X6,
  input  X7,
  input  A,
  input  B,
  input  C,
  output out_12
);

  wire and_1_out, and_2_out, and_3_out, and_4_out, and_5_out, and_6_out, and_7_out, and_8_out, not_1_out,
       not_2_out, not_3_out;

  not not_1 (not_1_out, A);
  not not_2 (not_2_out, B);
  not not_3 (not_3_out, C);
  and and_1 (and_1_out, X0, not_1_out, not_2_out, not_3_out);
  and and_2 (and_2_out, X1, not_1_out, not_2_out, C);
  and and_3 (and_3_out, X2, not_1_out, B, not_3_out);
  and and_4 (and_4_out, X3, not_1_out, B, C);
  and and_5 (and_5_out, X4, A, not_2_out, not_3_out);
  and and_6 (and_6_out, X5, A, not_2_out, C);
  and and_7 (and_7_out, X6, A, B, not_3_out);
  and and_8 (and_8_out, X7, A, B, C);
  or or_1 (out_12, and_1_out, and_2_out, and_3_out, and_4_out, and_5_out, and_6_out, and_7_out, and_8_out);
endmodule

module \Мультиплексор_с_3_мя_управляющими_контактами  (
  input  in_1,
  input  in_2,
  input  in_3,
  input  in_4,
  input  in_5,
  input  in_6,
  input  in_7,
  input  in_8,
  input  in_9,
  input  in_10,
  input  in_11
);

  wire \мультиплексор_1_out_12 ;

  \Мультиплексор  \u_мультиплексор_1  (
    .X0(in_1), .X1(in_2), .X2(in_3), .X3(in_4), .X4(in_5), .X5(in_6), .X6(in_7), .X7(in_8),
    .out_12(\мультиплексор_1_out_12 ), .A(in_11), .B(in_10), .C(in_9));
endmodule

module \Демультиплексор  (
  input  Input,
  input  A,
  input  B,
  input  C,
  output out_5,
  output out_6,
  output out_7,
  output out_8,
  output out_9,
  output out_10,
  output out_11,
  output out_12
);

  wire not_1_out, not_2_out, not_3_out;

  not not_1 (not_1_out, A);
  not not_2 (not_2_out, B);
  not not_3 (not_3_out, C);
  and _0 (out_5, Input, not_1_out, not_2_out, not_3_out);
  and _1 (out_6, Input, not_1_out, not_2_out, C);
  and _2 (out_7, Input, not_1_out, B, not_3_out);
  and _3 (out_8, Input, not_1_out, B, C);
  and _4 (out_9, Input, A, not_2_out, not_3_out);
  and _5 (out_10, Input, A, not_2_out, C);
  and _6 (out_11, Input, A, B, not_3_out);
  and _7 (out_12, Input, A, B, C);
endmodule

module \Демультиплексор_с_3_мя_управляющими_контактами  (
  input  in_1,
  input  in_2,
  input  in_3,
  input  in_4,
  output out_5,
  output out_6,
  output out_7,
  output out_8,
  output out_9,
  output out_10,
  output out_11,
  output out_12
);

  \Демультиплексор  \u_демультиплексор_1  (
    .Input(in_1), .out_5(out_5), .out_6(out_6), .out_7(out_7), .out_8(out_8), .out_9(out_9), .out_10(out_10),
    .out_11(out_11), .out_12(out_12), .A(in_4), .B(in_3), .C(in_2));
endmodule
