// Logisim project Lab_4_Triggers.circ as structural Verilog: 19 circuits, main circuit R/S - Триггер
module \R_S___Триггер  (
  input  Set,
  input  Reset,
  output Out_1,
  output Out_2
);

  wire and_1_out, and_2_out, not_1_out, not_2_out;

  not not_1 (not_1_out, Set);
  not not_2 (not_2_out, Reset);
  and and_1 (and_1_out, not_1_out, Out_2);
  and and_2 (and_2_out, Out_1, not_2_out);
  not not_3 (Out_1, and_1_out);
  not not_4 (Out_2, and_2_out);
endmodule

module \D___Триггер__Верхний_уровень__Сброс  (
  input  Clear,
  input  Clock,
  input  Data,
  output Out
);

  wire and_1_out, and_2_out, nor_2_out, not_1_out, or_1_out;

  not not_1 (not_1_out, Data);
  and and_1 (and_1_out, not_1_out, Clock);
  and and_2 (and_2_out, Clock, Data);
  or or_1 (or_1_out, Clear, and_1_out);
  nor nor_1 (Out, or_1_out, nor_2_out);
  nor nor_2 (nor_2_out, Out, and_2_out);
endmodule

module \D___Триггер__Верхний_уровень  (
  input  Clock,
  input  Data,
  output Out
);

  wire and_1_out, and_2_out, nor_2_out, not_1_out;

  not not_1 (not_1_out, Data);
  and and_1 (and_1_out, not_1_out, Clock);
  and and_2 (and_2_out, Clock, Data);
  nor nor_1 (Out, and_1_out, nor_2_out);
  nor nor_2 (nor_2_out, Out, and_2_out);
endmodule

module \D___Триггер__Нижний_уровень  (
  input  Clear,
  input  Clock,
  input  Data,
  output Out
);

  wire and_1_out, and_2_out, nor_2_out, not_1_out, not_2_out, or_1_out;

  not not_1 (not_1_out, Data);
  not not_2 (not_2_out, Clock);
  and and_1 (and_1_out, not_1_out, not_2_out);
  and and_2 (and_2_out, not_2_out, Data);
  or or_1 (or_1_out, Clear, and_1_out);
  nor nor_1 (Out, or_1_out, nor_2_out);
  nor nor_2 (nor_2_out, Out, and_2_out);
endmodule

module \D___Триггер__Задний_фронт  (
  input  Clock,
  input  Data,
  output Out
);

  wire and_1_out, and_2_out, and_3_out, and_4_out, nor_1_out, nor_2_out, nor_3_out, not_1_out, not_2_out;

  not not_1 (not_1_out, Clock);
  not not_2 (not_2_out, Data);
  and and_1 (and_1_out, not_2_out, Clock);
  and and_2 (and_2_out, Clock, Data);
  nor nor_1 (nor_1_out, and_1_out, nor_2_out);
  nor nor_2 (nor_2_out, nor_1_out, and_2_out);
  and and_3 (and_3_out, nor_1_out, not_1_out);
  and and_4 (and_4_out, not_1_out, nor_2_out);
  nor nor_3 (nor_3_out, and_3_out, Out);
  nor nor_4 (Out, nor_3_out, and_4_out);
endmodule

module \D___Триггер__Задний_фронт__Предустановка_Сброс  (
  input  Clear,
  input  Preset,
  input  Clock,
  input  Data,
  output out_5
);

  wire nor_1_out, nor_2_out, nor_3_out, nor_4_out, nor_6_out;

  nor nor_1 (nor_1_out, Clear, nor_4_out, nor_2_out);
  nor nor_2 (nor_2_out, nor_1_out, Preset, Clock);
  nor nor_3 (nor_3_out, nor_2_out, Clock, nor_4_out);
  nor nor_4 (nor_4_out, nor_3_out, Preset, Data);
  nor nor_5 (out_5, Clear, nor_2_out, nor_6_out);
  nor nor_6 (nor_6_out, out_5, Preset, nor_3_out);
endmodule

module \D___Триггер__Передний_фронт  (
  input  Clock,
  input  Data,
  output out_3,
  output out_4
);

  wire and_1_out, and_2_out, and_3_out, and_4_out, nor_1_out, nor_2_out, not_1_out, not_2_out;

  not not_1 (not_1_out, Data);
  not not_2 (not_2_out, Clock);
  and and_1 (and_1_out, not_1_out, not_2_out);
  and and_2 (and_2_out, not_2_out, Data);
  nor nor_1 (nor_1_out, and_1_out, nor_2_out);
  nor nor_2 (nor_2_out, nor_1_out, and_2_out);
  and and_3 (and_3_out, nor_1_out, Clock);
  and and_4 (and_4_out, Clock, nor_2_out);
  nor nor_3 (out_3, and_3_out, out_4);
  nor nor_4 (out_4, out_3, and_4_out);
endmodule

module \D___Триггер__Передний_фронт__Предустановка_Сброс  (
  input  Clear,
  input  Preset,
  input  Clock,
  input  Data,
  output out_5,
  output out_6
);

  wire nor_1_out, nor_2_out, nor_3_out, nor_4_out, not_1_out;

  not not_1 (not_1_out, Clock);
  nor nor_1 (nor_1_out, Clear, nor_4_out, nor_2_out);
  nor nor_2 (nor_2_out, nor_1_out, Preset, not_1_out);
  nor nor_3 (nor_3_out, nor_2_out, not_1_out, nor_4_out);
  nor nor_4 (nor_4_out, nor_3_out, Preset, Data);
  nor nor_5 (out_5, Clear, nor_2_out, out_6);
  nor nor_6 (out_6, out_5, Preset, nor_3_out);
endmodule

module \T___Триггер__Из_D___Триггера  (
  input  Clock,
  input  Preset,
  input  Clear
);

  wire \d_триггер_передний_фронт_предустановка_сброс_1_out_6 ,
       \d_триггер_передний_фронт_предустановка_сброс_2_out_6 ,
       \d_триггер_передний_фронт_предустановка_сброс_3_out_6 ,
       \d_триггер_передний_фронт_предустановка_сброс_4_out_6 ;
  wire [3:0] \d_триггер_передний_фронт_предустановка_сброс_1_out_5 ;

  // Probe on \d_триггер_передний_фронт_предустановка_сброс_1_out_5 
  \D___Триггер__Передний_фронт__Предустановка_Сброс  \d_триггер_передний_фронт_предустановка_сброс_1  (
    .Clear(Preset), .Preset(Clear), .Clock(Clock),
    .Data(\d_триггер_передний_фронт_предустановка_сброс_1_out_6 ),
    .out_5(\d_триггер_передний_фронт_предустановка_сброс_1_out_5 [0]),
    .out_6(\d_триггер_передний_фронт_предустановка_сброс_1_out_6 ));
  \D___Триггер__Передний_фронт__Предустановка_Сброс  \d_триггер_передний_фронт_предустановка_сброс_2  (
    .Clear(Preset), .Preset(Clear), .Clock(\d_триггер_передний_фронт_предустановка_сброс_1_out_5 [0]),
    .Data(\d_триггер_передний_фронт_предустановка_сброс_2_out_6 ),
    .out_5(\d_триггер_передний_фронт_предустановка_сброс_1_out_5 [1]),
    .out_6(\d_триггер_передний_фронт_предустановка_сброс_2_out_6 ));
  \D___Триггер__Передний_фронт__Предустановка_Сброс  \d_триггер_передний_фронт_предустановка_сброс_3  (
    .Clear(Preset), .Preset(Clear), .Clock(\d_триггер_передний_фронт_предустановка_сброс_1_out_5 [1]),
    .Data(\d_триггер_передний_фронт_предустановка_сброс_3_out_6 ),
    .out_5(\d_триггер_передний_фронт_предустановка_сброс_1_out_5 [2]),
    .out_6(\d_триггер_передний_фронт_предустановка_сброс_3_out_6 ));
  \D___Триггер__Передний_фронт__Предустановка_Сброс  \d_триггер_передний_фронт_предустановка_сброс_4  (
    .Clear(Preset), .Preset(Clear), .Clock(\d_триггер_передний_фронт_предустановка_сброс_1_out_5 [2]),
    .Data(\d_триггер_передний_фронт_предустановка_сброс_4_out_6 ),
    .out_5(\d_триггер_передний_фронт_предустановка_сброс_1_out_5 [3]),
    .out_6(\d_триггер_передний_фронт_предустановка_сброс_4_out_6 ));
endmodule

module \JK___Триггер__Из_D___Триггера  (
  input  K,
  input  J,
  input  Clock,
  input  Preset,
  input  Clear,
  output out_6,
  output out_7
);

  wire and_1_out, and_2_out, not_1_out, or_1_out;

  not not_1 (not_1_out, K);
  and and_1 (and_1_out, out_6, not_1_out);
  or or_1 (or_1_out, and_1_out, and_2_out);
  and and_2 (and_2_out, J, out_7);
  \D___Триггер__Передний_фронт__Предустановка_Сброс  \d_триггер_передний_фронт_предустановка_сброс_1  (
    .Clear(Preset), .Preset(Clear), .Clock(Clock), .Data(or_1_out), .out_5(out_6), .out_6(out_7));
endmodule

module \TC___Триггер__Из_D___Триггера  (
  input  T,
  input  C,
  input  Preset,
  input  Clear,
  output out_5
);

  wire \d_триггер_передний_фронт_предустановка_сброс_1_out_5 , xor_1_out;

  xor xor_1 (xor_1_out, \d_триггер_передний_фронт_предустановка_сброс_1_out_5 , T);
  \D___Триггер__Передний_фронт__Предустановка_Сброс  \d_триггер_передний_фронт_предустановка_сброс_1  (
    .Clear(Preset), .Preset(Clear), .Clock(C), .Data(xor_1_out),
    .out_5(\d_триггер_передний_фронт_предустановка_сброс_1_out_5 ), .out_6(out_5));
endmodule

module \Восьмибитный_регистр__Асинхронный  (
  input  Save,
  input  [7:0] in_2,
  output [7:0] out_3
);

  D_Flip_Flop d_ff_1 (.clk(Save), .D(in_2[0]), .Q(out_3[0]));  // open: Qn, preset, en, reset
  D_Flip_Flop d_ff_2 (.clk(Save), .D(in_2[1]), .Q(out_3[1]));  // open: Qn, preset, en, reset
  D_Flip_Flop d_ff_3 (.clk(Save), .D(in_2[2]), .Q(out_3[2]));  // open: Qn, preset, en, reset
  D_Flip_Flop d_ff_4 (.clk(Save), .D(in_2[3]), .Q(out_3[3]));  // open: Qn, preset, en, reset
  D_Flip_Flop d_ff_5 (.clk(Save), .D(in_2[4]), .Q(out_3[4]));  // open: Qn, preset, en, reset
  D_Flip_Flop d_ff_6 (.clk(Save), .D(in_2[5]), .Q(out_3[5]));  // open: Qn, preset, en, reset
  D_Flip_Flop d_ff_7 (.clk(Save), .D(in_2[6]), .Q(out_3[6]));  // open: Qn, preset, en, reset
  D_Flip_Flop d_ff_8 (.clk(Save), .D(in_2[7]), .Q(out_3[7]));  // open: Qn, preset, en, reset
endmodule

module \Восьмибитный_регистр__Синхронный  (
  input  [7:0] in_1,
  input  Write,
  input  Clear,
  output [7:0] out_4
);

  wire clock_1_out;

  Clock clock_1 (.out(clock_1_out));
  D_Flip_Flop d_ff_1 (.clk(clock_1_out), .D(in_1[0]), .Q(out_4[0]), .en(Write), .reset(Clear));  // open: Qn, preset
  D_Flip_Flop d_ff_2 (.clk(clock_1_out), .D(in_1[1]), .Q(out_4[1]), .en(Write), .reset(Clear));  // open: Qn, preset
  D_Flip_Flop d_ff_3 (.clk(clock_1_out), .D(in_1[2]), .Q(out_4[2]), .en(Write), .reset(Clear));  // open: Qn, preset
  D_Flip_Flop d_ff_4 (.clk(clock_1_out), .D(in_1[3]), .Q(out_4[3]), .en(Write), .reset(Clear));  // open: Qn, preset
  D_Flip_Flop d_ff_5 (.clk(clock_1_out), .D(in_1[4]), .Q(out_4[4]), .en(Write), .reset(Clear));  // open: Qn, preset
  D_Flip_Flop d_ff_6 (.clk(clock_1_out), .D(in_1[5]), .Q(out_4[5]), .en(Write), .reset(Clear));  // open: Qn, preset
  D_Flip_Flop d_ff_7 (.clk(clock_1_out), .D(in_1[6]), .Q(out_4[6]), .en(Write), .reset(Clear));  // open: Qn, preset
  D_Flip_Flop d_ff_8 (.clk(clock_1_out), .D(in_1[7]), .Q(out_4[7]), .en(Write), .reset(Clear));  // open: Qn, preset
endmodule

module \Память_на_1024_ячейки  (
  input  [7:0] in_1,
  input  in_2,
  input  [4:0] in_3,
  output [7:0] out_4
);

  wire demultiplexer_1_out0, demultiplexer_1_out1, demultiplexer_1_out2, demultiplexer_1_out3,
       demultiplexer_1_out4, demultiplexer_1_out5, demultiplexer_1_out6, demultiplexer_1_out7,
       demultiplexer_1_out8, demultiplexer_1_out9, demultiplexer_1_out10, demultiplexer_1_out11,
       demultiplexer_1_out12, demultiplexer_1_out13, demultiplexer_1_out14, demultiplexer_1_out15,
       demultiplexer_1_out16, demultiplexer_1_out17, demultiplexer_1_out18, demultiplexer_1_out19,
       demultiplexer_1_out20, demultiplexer_1_out21, demultiplexer_1_out22, demultiplexer_1_out23,
       demultiplexer_1_out24, demultiplexer_1_out25, demultiplexer_1_out26, demultiplexer_1_out27,
       demultiplexer_1_out28, demultiplexer_1_out29, demultiplexer_1_out30, demultiplexer_1_out31;
  wire [7:0] \восьмибитный_регистр_асинхронный_1_out_3 , \восьмибитный_регистр_асинхронный_2_out_3 ,
       \восьмибитный_регистр_асинхронный_3_out_3 , \восьмибитный_регистр_асинхронный_4_out_3 ,
       \восьмибитный_регистр_асинхронный_5_out_3 , \восьмибитный_регистр_асинхронный_6_out_3 ,
       \восьмибитный_регистр_асинхронный_7_out_3 , \восьмибитный_регистр_асинхронный_8_out_3 ,
       \восьмибитный_регистр_асинхронный_9_out_3 , \восьмибитный_регистр_асинхронный_10_out_3 ,
       \восьмибитный_регистр_асинхронный_11_out_3 , \восьмибитный_регистр_асинхронный_12_out_3 ,
       \восьмибитный_регистр_асинхронный_13_out_3 , \восьмибитный_регистр_асинхронный_14_out_3 ,
       \восьмибитный_регистр_асинхронный_15_out_3 , \восьмибитный_регистр_асинхронный_16_out_3 ,
       \восьмибитный_регистр_асинхронный_17_out_3 , \восьмибитный_регистр_асинхронный_18_out_3 ,
       \восьмибитный_регистр_асинхронный_19_out_3 , \восьмибитный_регистр_асинхронный_20_out_3 ,
       \восьмибитный_регистр_асинхронный_21_out_3 , \восьмибитный_регистр_асинхронный_22_out_3 ,
       \восьмибитный_регистр_асинхронный_23_out_3 , \восьмибитный_регистр_асинхронный_24_out_3 ,
       \восьмибитный_регистр_асинхронный_25_out_3 , \восьмибитный_регистр_асинхронный_26_out_3 ,
       \восьмибитный_регистр_асинхронный_27_out_3 , \восьмибитный_регистр_асинхронный_28_out_3 ,
       \восьмибитный_регистр_асинхронный_29_out_3 , \восьмибитный_регистр_асинхронный_30_out_3 ,
       \восьмибитный_регистр_асинхронный_31_out_3 , \восьмибитный_регистр_асинхронный_32_out_3 ;

  Demultiplexer #(.select(5)) demultiplexer_1 (
    .out0(demultiplexer_1_out0), .out1(demultiplexer_1_out1), .out2(demultiplexer_1_out2),
    .out3(demultiplexer_1_out3), .out4(demultiplexer_1_out4), .out5(demultiplexer_1_out5),
    .out6(demultiplexer_1_out6), .out7(demultiplexer_1_out7), .out8(demultiplexer_1_out8),
    .out9(demultiplexer_1_out9), .out10(demultiplexer_1_out10), .out11(demultiplexer_1_out11),
    .out12(demultiplexer_1_out12), .out13(demultiplexer_1_out13), .out14(demultiplexer_1_out14),
    .out15(demultiplexer_1_out15), .out16(demultiplexer_1_out16), .out17(demultiplexer_1_out17),
    .out18(demultiplexer_1_out18), .out19(demultiplexer_1_out19), .out20(demultiplexer_1_out20),
    .out21(demultiplexer_1_out21), .out22(demultiplexer_1_out22), .out23(demultiplexer_1_out23),
    .out24(demultiplexer_1_out24), .out25(demultiplexer_1_out25), .out26(demultiplexer_1_out26),
    .out27(demultiplexer_1_out27), .out28(demultiplexer_1_out28), .out29(demultiplexer_1_out29),
    .out30(demultiplexer_1_out30), .out31(demultiplexer_1_out31), .in(in_2), .sel(in_3));  // open: en
  // Probe on \восьмибитный_регистр_асинхронный_1_out_3 
  // Probe on \восьмибитный_регистр_асинхронный_2_out_3 
  // Probe on \восьмибитный_регистр_асинхронный_3_out_3 
  // Probe on \восьмибитный_регистр_асинхронный_4_out_3 
  // Probe on \восьмибитный_регистр_асинхронный_5_out_3 
  // Probe on \восьмибитный_регистр_асинхронный_6_out_3 
  // Probe on \восьмибитный_регистр_асинхронный_7_out_3 
  // Probe on \восьмибитный_регистр_асинхронный_8_out_3 
  \Восьмибитный_регистр__Асинхронный  \u_восьмибитный_регистр_асинхронный_1  (
    .Save(demultiplexer_1_out0), .in_2(in_1), .out_3(\восьмибитный_регистр_асинхронный_1_out_3 ));
  \Восьмибитный_регистр__Асинхронный  \u_восьмибитный_регистр_асинхронный_2  (
    .Save(demultiplexer_1_out4), .in_2(in_1), .out_3(\восьмибитный_регистр_асинхронный_2_out_3 ));
  \Восьмибитный_регистр__Асинхронный  \u_восьмибитный_регистр_асинхронный_3  (
    .Save(demultiplexer_1_out8), .in_2(in_1), .out_3(\восьмибитный_регистр_асинхронный_3_out_3 ));
  \Восьмибитный_регистр__Асинхронный  \u_восьмибитный_регистр_асинхронный_4  (
    .Save(demultiplexer_1_out12), .in_2(in_1), .out_3(\восьмибитный_регистр_асинхронный_4_out_3 ));
  \Восьмибитный_регистр__Асинхронный  \u_восьмибитный_регистр_асинхронный_5  (
    .Save(demultiplexer_1_out16), .in_2(in_1), .out_3(\восьмибитный_регистр_асинхронный_5_out_3 ));
  \Восьмибитный_регистр__Асинхронный  \u_восьмибитный_регистр_асинхронный_6  (
    .Save(demultiplexer_1_out20), .in_2(in_1), .out_3(\восьмибитный_регистр_асинхронный_6_out_3 ));
  \Восьмибитный_регистр__Асинхронный  \u_восьмибитный_регистр_асинхронный_7  (
    .Save(demultiplexer_1_out24), .in_2(in_1), .out_3(\восьмибитный_регистр_асинхронный_7_out_3 ));
  \Восьмибитный_регистр__Асинхронный  \u_восьмибитный_регистр_асинхронный_8  (
    .Save(demultiplexer_1_out28), .in_2(in_1), .out_3(\восьмибитный_регистр_асинхронный_8_out_3 ));
  // Probe on \восьмибитный_регистр_асинхронный_9_out_3 
  // Probe on \восьмибитный_регистр_асинхронный_10_out_3 
  // Probe on \восьмибитный_регистр_асинхронный_11_out_3 
  // Probe on \восьмибитный_регистр_асинхронный_12_out_3 
  // Probe on \восьмибитный_регистр_асинхронный_13_out_3 
  // Probe on \восьмибитный_регистр_асинхронный_14_out_3 
  // Probe on \восьмибитный_регистр_асинхронный_15_out_3 
  // Probe on \восьмибитный_регистр_асинхронный_16_out_3 
  \Восьмибитный_регистр__Асинхронный  \u_восьмибитный_регистр_асинхронный_9  (
    .Save(demultiplexer_1_out1), .in_2(in_1), .out_3(\восьмибитный_регистр_асинхронный_9_out_3 ));
  \Восьмибитный_регистр__Асинхронный  \u_восьмибитный_регистр_асинхронный_10  (
    .Save(demultiplexer_1_out5), .in_2(in_1), .out_3(\восьмибитный_регистр_асинхронный_10_out_3 ));
  \Восьмибитный_регистр__Асинхронный  \u_восьмибитный_регистр_асинхронный_11  (
    .Save(demultiplexer_1_out9), .in_2(in_1), .out_3(\восьмибитный_регистр_асинхронный_11_out_3 ));
  \Восьмибитный_регистр__Асинхронный  \u_восьмибитный_регистр_асинхронный_12  (
    .Save(demultiplexer_1_out13), .in_2(in_1), .out_3(\восьмибитный_регистр_асинхронный_12_out_3 ));
  \Восьмибитный_регистр__Асинхронный  \u_восьмибитный_регистр_асинхронный_13  (
    .Save(demultiplexer_1_out17), .in_2(in_1), .out_3(\восьмибитный_регистр_асинхронный_13_out_3 ));
  \Восьмибитный_регистр__Асинхронный  \u_восьмибитный_регистр_асинхронный_14  (
    .Save(demultiplexer_1_out21), .in_2(in_1), .out_3(\восьмибитный_регистр_асинхронный_14_out_3 ));
  \Восьмибитный_регистр__Асинхронный  \u_восьмибитный_регистр_асинхронный_15  (
    .Save(demultiplexer_1_out25), .in_2(in_1), .out_3(\восьмибитный_регистр_асинхронный_15_out_3 ));
  \Восьмибитный_регистр__Асинхронный  \u_восьмибитный_регистр_асинхронный_16  (
    .Save(demultiplexer_1_out29), .in_2(in_1), .out_3(\восьмибитный_регистр_асинхронный_16_out_3 ));
  // Probe on \восьмибитный_регистр_асинхронный_17_out_3 
  // Probe on \восьмибитный_регистр_асинхронный_18_out_3 
  // Probe on \восьмибитный_регистр_асинхронный_19_out_3 
  // Probe on \восьмибитный_регистр_асинхронный_20_out_3 
  // Probe on \восьмибитный_регистр_асинхронный_21_out_3 
  // Probe on \восьмибитный_регистр_асинхронный_22_out_3 
  // Probe on \восьмибитный_регистр_асинхронный_23_out_3 
  // Probe on \восьмибитный_регистр_асинхронный_24_out_3 
  \Восьмибитный_регистр__Асинхронный  \u_восьмибитный_регистр_асинхронный_17  (
    .Save(demultiplexer_1_out2), .in_2(in_1), .out_3(\восьмибитный_регистр_асинхронный_17_out_3 ));
  \Восьмибитный_регистр__Асинхронный  \u_восьмибитный_регистр_асинхронный_18  (
    .Save(demultiplexer_1_out6), .in_2(in_1), .out_3(\восьмибитный_регистр_асинхронный_18_out_3 ));
  \Восьмибитный_регистр__Асинхронный  \u_восьмибитный_регистр_асинхронный_19  (
    .Save(demultiplexer_1_out10), .in_2(in_1), .out_3(\восьмибитный_регистр_асинхронный_19_out_3 ));
  \Восьмибитный_регистр__Асинхронный  \u_восьмибитный_регистр_асинхронный_20  (
    .Save(demultiplexer_1_out14), .in_2(in_1), .out_3(\восьмибитный_регистр_асинхронный_20_out_3 ));
  \Восьмибитный_регистр__Асинхронный  \u_восьмибитный_регистр_асинхронный_21  (
    .Save(demultiplexer_1_out18), .in_2(in_1), .out_3(\восьмибитный_регистр_асинхронный_21_out_3 ));
  \Восьмибитный_регистр__Асинхронный  \u_восьмибитный_регистр_асинхронный_22  (
    .Save(demultiplexer_1_out22), .in_2(in_1), .out_3(\восьмибитный_регистр_асинхронный_22_out_3 ));
  \Восьмибитный_регистр__Асинхронный  \u_восьмибитный_регистр_асинхронный_23  (
    .Save(demultiplexer_1_out26), .in_2(in_1), .out_3(\восьмибитный_регистр_асинхронный_23_out_3 ));
  \Восьмибитный_регистр__Асинхронный  \u_восьмибитный_регистр_асинхронный_24  (
    .Save(demultiplexer_1_out30), .in_2(in_1), .out_3(\восьмибитный_регистр_асинхронный_24_out_3 ));
  \Восьмибитный_регистр__Асинхронный  \u_восьмибитный_регистр_асинхронный_25  (
    .Save(demultiplexer_1_out3), .in_2(in_1), .out_3(\восьмибитный_регистр_асинхронный_25_out_3 ));
  // Probe on \восьмибитный_регистр_асинхронный_25_out_3 
  \Восьмибитный_регистр__Асинхронный  \u_восьмибитный_регистр_асинхронный_26  (
    .Save(demultiplexer_1_out7), .in_2(in_1), .out_3(\восьмибитный_регистр_асинхронный_26_out_3 ));
  // Probe on \восьмибитный_регистр_асинхронный_26_out_3 
  \Восьмибитный_регистр__Асинхронный  \u_восьмибитный_регистр_асинхронный_27  (
    .Save(demultiplexer_1_out11), .in_2(in_1), .out_3(\восьмибитный_регистр_асинхронный_27_out_3 ));
  // Probe on \восьмибитный_регистр_асинхронный_27_out_3 
  \Восьмибитный_регистр__Асинхронный  \u_восьмибитный_регистр_асинхронный_28  (
    .Save(demultiplexer_1_out15), .in_2(in_1), .out_3(\восьмибитный_регистр_асинхронный_28_out_3 ));
  // Probe on \восьмибитный_регистр_асинхронный_28_out_3 
  \Восьмибитный_регистр__Асинхронный  \u_восьмибитный_регистр_асинхронный_29  (
    .Save(demultiplexer_1_out19), .in_2(in_1), .out_3(\восьмибитный_регистр_асинхронный_29_out_3 ));
  // Probe on \восьмибитный_регистр_асинхронный_29_out_3 
  \Восьмибитный_регистр__Асинхронный  \u_восьмибитный_регистр_асинхронный_30  (
    .Save(demultiplexer_1_out23), .out_3(\восьмибитный_регистр_асинхронный_30_out_3 ));  // open: in_2
  // Probe on \восьмибитный_регистр_асинхронный_30_out_3 
  \Восьмибитный_регистр__Асинхронный  \u_восьмибитный_регистр_асинхронный_31  (
    .Save(demultiplexer_1_out27), .in_2(in_1), .out_3(\восьмибитный_регистр_асинхронный_31_out_3 ));
  // Probe on \восьмибитный_регистр_асинхронный_31_out_3 
  \Восьмибитный_регистр__Асинхронный  \u_восьмибитный_регистр_асинхронный_32  (
    .Save(demultiplexer_1_out31), .in_2(in_1), .out_3(\восьмибитный_регистр_асинхронный_32_out_3 ));
  // Probe on \восьмибитный_регистр_асинхронный_32_out_3 
  Multiplexer #(.select(5), .width(8)) multiplexer_1 (
    .in0(\восьмибитный_регистр_асинхронный_1_out_3 ), .in1(\восьмибитный_регистр_асинхронный_9_out_3 ),
    .in2(\восьмибитный_регистр_асинхронный_17_out_3 ), .in3(\восьмибитный_регистр_асинхронный_25_out_3 ),
    .in4(\восьмибитный_регистр_асинхронный_2_out_3 ), .in5(\восьмибитный_регистр_асинхронный_10_out_3 ),
    .in6(\восьмибитный_регистр_асинхронный_18_out_3 ), .in7(\восьмибитный_регистр_асинхронный_26_out_3 ),
    .in8(\восьмибитный_регистр_асинхронный_3_out_3 ), .in9(\восьмибитный_регистр_асинхронный_11_out_3 ),
    .in10(\восьмибитный_регистр_асинхронный_19_out_3 ), .in11(\восьмибитный_регистр_асинхронный_27_out_3 ),
    .in12(\восьмибитный_регистр_асинхронный_4_out_3 ), .in13(\восьмибитный_регистр_асинхронный_12_out_3 ),
    .in14(\восьмибитный_регистр_асинхронный_20_out_3 ), .in15(\восьмибитный_регистр_асинхронный_28_out_3 ),
    .in16(\восьмибитный_регистр_асинхронный_5_out_3 ), .in17(\восьмибитный_регистр_асинхронный_13_out_3 ),
    .in18(\восьмибитный_регистр_асинхронный_21_out_3 ), .in19(\восьмибитный_регистр_асинхронный_29_out_3 ),
    .in20(\восьмибитный_регистр_асинхронный_6_out_3 ), .in21(\восьмибитный_регистр_асинхронный_14_out_3 ),
    .in22(\восьмибитный_регистр_асинхронный_22_out_3 ), .in23(\восьмибитный_регистр_асинхронный_30_out_3 ),
    .in24(\восьмибитный_регистр_асинхронный_7_out_3 ), .in25(\восьмибитный_регистр_асинхронный_15_out_3 ),
    .in26(\восьмибитный_регистр_асинхронный_23_out_3 ), .in27(\восьмибитный_регистр_асинхронный_31_out_3 ),
    .in28(\восьмибитный_регистр_асинхронный_8_out_3 ), .in29(\восьмибитный_регистр_асинхронный_16_out_3 ),
    .in30(\восьмибитный_регистр_асинхронный_24_out_3 ), .in31(\восьмибитный_регистр_асинхронный_32_out_3 ),
    .out(out_4), .sel(in_3));  // open: en
endmodule

module \Асинхронный_счётчик  (
  input  in_1,
  input  in_2,
  output [7:0] out_3
);

  wire d_ff_1_qn, d_ff_2_qn, d_ff_3_qn, d_ff_4_qn, d_ff_5_qn, d_ff_6_qn, d_ff_7_qn, d_ff_8_qn;

  D_Flip_Flop d_ff_1 (.clk(in_1), .D(d_ff_1_qn), .Q(out_3[0]), .Qn(d_ff_1_qn), .reset(in_2));  // open: preset, en
  D_Flip_Flop d_ff_2 (.clk(d_ff_1_qn), .D(d_ff_2_qn), .Q(out_3[1]), .Qn(d_ff_2_qn), .reset(in_2));  // open: preset, en
  // Probe on out_3
  D_Flip_Flop d_ff_3 (.clk(d_ff_2_qn), .D(d_ff_3_qn), .Q(out_3[2]), .Qn(d_ff_3_qn), .reset(in_2));  // open: preset, en
  D_Flip_Flop d_ff_4 (.clk(d_ff_3_qn), .D(d_ff_4_qn), .Q(out_3[3]), .Qn(d_ff_4_qn), .reset(in_2));  // open: preset, en
  D_Flip_Flop d_ff_5 (.clk(d_ff_4_qn), .D(d_ff_5_qn), .Q(out_3[4]), .Qn(d_ff_5_qn), .reset(in_2));  // open: preset, en
  D_Flip_Flop d_ff_6 (.clk(d_ff_5_qn), .D(d_ff_6_qn), .Q(out_3[5]), .Qn(d_ff_6_qn), .reset(in_2));  // open: preset, en
  D_Flip_Flop d_ff_7 (.clk(d_ff_6_qn), .D(d_ff_7_qn), .Q(out_3[6]), .Qn(d_ff_7_qn), .reset(in_2));  // open: preset, en
  D_Flip_Flop d_ff_8 (.clk(d_ff_7_qn), .D(d_ff_8_qn), .Q(out_3[7]), .Qn(d_ff_8_qn), .reset(in_2));  // open: preset, en
endmodule

module \Асинхронный_обратынй_счётчик  (
  input  in_1,
  input  in_2,
  output [7:0] out_3
);

  wire d_ff_1_qn, d_ff_2_qn, d_ff_3_qn, d_ff_4_qn, d_ff_5_qn, d_ff_6_qn, d_ff_7_qn, d_ff_8_qn;

  D_Flip_Flop d_ff_1 (.clk(in_1), .D(d_ff_1_qn), .Q(out_3[0]), .Qn(d_ff_1_qn), .reset(in_2));  // open: preset, en
  D_Flip_Flop d_ff_2 (.clk(out_3[0]), .D(d_ff_2_qn), .Q(out_3[1]), .Qn(d_ff_2_qn), .reset(in_2));  // open: preset, en
  // Probe on out_3
  D_Flip_Flop d_ff_3 (.clk(out_3[1]), .D(d_ff_3_qn), .Q(out_3[2]), .Qn(d_ff_3_qn), .reset(in_2));  // open: preset, en
  D_Flip_Flop d_ff_4 (.clk(out_3[2]), .D(d_ff_4_qn), .Q(out_3[3]), .Qn(d_ff_4_qn), .reset(in_2));  // open: preset, en
  D_Flip_Flop d_ff_5 (.clk(out_3[3]), .D(d_ff_5_qn), .Q(out_3[4]), .Qn(d_ff_5_qn), .reset(in_2));  // open: preset, en
  D_Flip_Flop d_ff_6 (.clk(out_3[4]), .D(d_ff_6_qn), .Q(out_3[5]), .Qn(d_ff_6_qn), .reset(in_2));  // open: preset, en
  D_Flip_Flop d_ff_7 (.clk(out_3[5]), .D(d_ff_7_qn), .Q(out_3[6]), .Qn(d_ff_7_qn), .reset(in_2));  // open: preset, en
  D_Flip_Flop d_ff_8 (.clk(out_3[6]), .D(d_ff_8_qn), .Q(out_3[7]), .Qn(d_ff_8_qn), .reset(in_2));  // open: preset, en
endmodule

module \Полусумматор  (
  input  A,
  input  B,
  output Out,
  output P
);

  xor xor_1 (Out, A, B);
  and and_1 (P, A, B);
endmodule

module \Сумматор  (
  input  P,
  input  A,
  input  B,
  output out_4,
  output out_5
);

  wire \полусумматор_1_out , \полусумматор_1_p , \полусумматор_2_p ;

  \Полусумматор  \u_полусумматор_1  (.A(A), .B(B), .Out(\полусумматор_1_out ), .P(\полусумматор_1_p ));
  \Полусумматор  \u_полусумматор_2  (.A(P), .B(\полусумматор_1_out ), .Out(out_4), .P(\полусумматор_2_p ));
  or or_1 (out_5, \полусумматор_2_p , \полусумматор_1_p );
endmodule

module \Восьмибитный_сумматор  (
  input  \Использовать ,
  input  [7:0] in_2,
  input  [7:0] in_3,
  input  in_4
);

  wire button_1_out, \сумматор_1_out_5 , \сумматор_2_out_5 , \сумматор_3_out_5 , \сумматор_4_out_5 ,
       \сумматор_5_out_5 , \сумматор_6_out_5 , \сумматор_7_out_5 ;
  wire [7:0] multiplexer_1_out, transistor_1_out, \восьмибитный_регистр_асинхронный_1_out_3 ,
       \сумматор_1_out_4 ;

  Transistor #(.width(8)) transistor_1 (.in(in_3), .out(transistor_1_out), .gate(\Использовать ));
  Transistor #(.\type ("n"), .width(8)) transistor_2 (
    .in(multiplexer_1_out), .out(transistor_1_out), .gate(\Использовать ));
  // Probe on in_2
  Multiplexer #(.width(8)) multiplexer_1 (
    .in0(transistor_1_out), .in1(\восьмибитный_регистр_асинхронный_1_out_3 ), .out(multiplexer_1_out),
    .sel(\Использовать ));  // open: en
  // Probe on multiplexer_1_out
  // Probe on \сумматор_1_out_4 
  // Probe on \сумматор_1_out_4 
  \Сумматор  \u_сумматор_1  (
    .P(in_4), .A(in_2[0]), .B(transistor_1_out[0]), .out_4(\сумматор_1_out_4 [0]), .out_5(\сумматор_1_out_5 ));
  \Сумматор  \u_сумматор_2  (
    .P(\сумматор_1_out_5 ), .A(in_2[1]), .B(transistor_1_out[1]), .out_4(\сумматор_1_out_4 [1]),
    .out_5(\сумматор_2_out_5 ));
  \Сумматор  \u_сумматор_3  (
    .P(\сумматор_2_out_5 ), .A(in_2[2]), .B(transistor_1_out[2]), .out_4(\сумматор_1_out_4 [2]),
    .out_5(\сумматор_3_out_5 ));
  \Сумматор  \u_сумматор_4  (
    .P(\сумматор_3_out_5 ), .A(in_2[3]), .B(transistor_1_out[3]), .out_4(\сумматор_1_out_4 [3]),
    .out_5(\сумматор_4_out_5 ));
  \Сумматор  \u_сумматор_5  (
    .P(\сумматор_4_out_5 ), .A(in_2[4]), .B(transistor_1_out[4]), .out_4(\сумматор_1_out_4 [4]),
    .out_5(\сумматор_5_out_5 ));
  \Сумматор  \u_сумматор_6  (
    .P(\сумматор_5_out_5 ), .A(in_2[5]), .B(transistor_1_out[5]), .out_4(\сумматор_1_out_4 [5]),
    .out_5(\сумматор_6_out_5 ));
  \Сумматор  \u_сумматор_7  (
    .P(\сумматор_6_out_5 ), .A(in_2[6]), .B(transistor_1_out[6]), .out_4(\сумматор_1_out_4 [6]),
    .out_5(\сумматор_7_out_5 ));
  \Сумматор  \u_сумматор_8  (
    .P(\сумматор_7_out_5 ), .A(in_2[7]), .B(transistor_1_out[7]), .out_4(\сумматор_1_out_4 [7]));  // open: out_5
  Button button_1 (.out(button_1_out));
  \Восьмибитный_регистр__Асинхронный  \u_восьмибитный_регистр_асинхронный_1  (
    .Save(button_1_out), .in_2(\сумматор_1_out_4 ), .out_3(\восьмибитный_регистр_асинхронный_1_out_3 ));
  // Probe on \восьмибитный_регистр_асинхронный_1_out_3 

  // Notes on the sheet:
  //   +
  //   =
  //   ↑
  //   Запомнить число
  //   Число из памяти
endmodule
