// Logisim project Svetofor_lab.circ as structural Verilog: 2 circuits, main circuit Светофор
module \Светофор  (
  input  ta,
  input  tb,
  input  \Сброс 
);

  wire and_1_out, and_2_out, and_3_out, and_4_out, and_5_out, and_6_out, and_7_out, and_8_out, clock_1_out,
       d_ff_1_q, d_ff_1_qn, d_ff_2_q, d_ff_2_qn, not_1_out, not_2_out, not_3_out, not_4_out, not_5_out,
       not_6_out, not_7_out, not_8_out, not_9_out, not_10_out, not_11_out, not_12_out, not_13_out, or_1_out,
       or_2_out, or_3_out, or_4_out;

  not not_1 (not_1_out, d_ff_1_q);
  not not_2 (not_2_out, d_ff_2_q);
  not not_3 (not_3_out, d_ff_1_q);
  not not_4 (not_4_out, d_ff_2_q);
  not not_5 (not_5_out, ta);
  not not_6 (not_6_out, d_ff_2_q);
  not not_7 (not_7_out, tb);
  and and_1 (and_1_out, not_1_out, d_ff_2_q);
  or or_1 (or_1_out, and_1_out, and_2_out);
  and and_2 (and_2_out, d_ff_1_q, not_2_out);
  and and_3 (and_3_out, not_3_out, not_4_out, not_5_out);
  or or_2 (or_2_out, and_3_out, and_4_out);
  and and_4 (and_4_out, d_ff_1_q, not_6_out, not_7_out);
  Clock clock_1 (.out(clock_1_out));
  D_Flip_Flop d_ff_1 (
    .clk(clock_1_out), .D(or_1_out), .Q(d_ff_1_q), .Qn(d_ff_1_qn), .reset(\Сброс ));  // open: preset, en
  D_Flip_Flop d_ff_2 (
    .clk(clock_1_out), .D(or_2_out), .Q(d_ff_2_q), .Qn(d_ff_2_qn), .reset(\Сброс ));  // open: preset, en
  not not_8 (not_8_out, d_ff_1_qn);
  not not_9 (not_9_out, d_ff_1_qn);
  and and_5 (and_5_out, not_8_out, d_ff_2_qn);
  not not_10 (not_10_out, and_5_out);
  not not_11 (not_11_out, d_ff_1_qn);
  and and_6 (and_6_out, d_ff_1_qn, d_ff_2_qn);
  not not_12 (not_12_out, not_9_out);
  not not_13 (not_13_out, and_6_out);
  LED led_1 (.in(d_ff_1_qn));
  LED led_2 (.in(and_7_out));
  and and_7 (and_7_out, not_10_out, not_11_out);
  LED led_3 (.in(and_5_out));
  LED led_4 (.in(not_9_out));
  LED led_5 (.in(and_8_out));
  and and_8 (and_8_out, not_12_out, not_13_out);
  LED led_6 (.in(and_6_out));
  or or_3 (or_3_out, and_7_out, and_5_out);
  LED led_7 (.in(or_3_out));
  LED led_8 (.in(d_ff_1_qn));
  or or_4 (or_4_out, and_6_out, and_8_out);
  LED led_9 (.in(or_4_out));
  LED led_10 (.in(not_9_out));

  // Notes on the sheet:
  //   Датчики
  //   движения
  //   Беговая 
  //   Академическая
  //   Светофор
  //   для
  //   пешеходов
  //   Светофор
  //   для
  //   транспорта
  //   Светофор
  //   для
  //   пешеходов
  //   Светофор
  //   для
  //   транспорта
endmodule

module min (
  input  s1,
  input  s0,
  input  ta,
  input  tb,
  output fs1,
  output fs0
);

  wire and_1_out, and_2_out, and_3_out, and_4_out, not_1_out, not_2_out, not_3_out, not_4_out, not_5_out,
       not_6_out, not_7_out;

  not not_1 (not_1_out, s1);
  and and_1 (and_1_out, not_1_out, s0);
  and and_2 (and_2_out, s1, not_2_out);
  not not_2 (not_2_out, s0);
  not not_3 (not_3_out, s1);
  and and_3 (and_3_out, not_3_out, not_4_out, not_5_out);
  not not_4 (not_4_out, s0);
  not not_5 (not_5_out, ta);
  and and_4 (and_4_out, s1, not_6_out, not_7_out);
  not not_6 (not_6_out, s0);
  not not_7 (not_7_out, tb);
  or or_1 (fs1, and_1_out, and_2_out);
  or or_2 (fs0, and_3_out, and_4_out);
endmodule
