// Logisim project Архитектура Фон Неймана.circ as structural Verilog: 1 circuit, main circuit main
module main (
);

  wire and_1_out, and_2_out, and_3_out, clock_1_out, not_1_out, not_2_out;
  wire [3:0] multiplexer_1_out, \Адрес_q , \Команда_q , \Счётчик_q ;
  wire [7:0] \Accum_сложение_q , adder_1_out, multiplexer_2_out, ram_1_data, \Промежуточный_результат_q ;

  not not_1 (not_1_out, \Команда_q [3]);
  Clock clock_1 (.out(clock_1_out));
  not not_2 (not_2_out, clock_1_out);
  Counter #(.width(4), .max('hf)) \u_Счётчик  (
    .D(\Адрес_q ), .count(not_1_out), .Q(\Счётчик_q ), .clk(clock_1_out), .clr(and_1_out));  // open: load, carry
  Multiplexer #(.width(4)) multiplexer_1 (
    .in0(\Счётчик_q ), .in1(\Адрес_q ), .out(multiplexer_1_out), .sel(not_2_out));  // open: en
  and and_1 (and_1_out, clock_1_out, clock_1_out, clock_1_out, \Команда_q [1]);
  and and_2 (and_2_out, clock_1_out, \Команда_q [1]);
  RAM #(.addrWidth(4), .bus("separate")) ram_1 (
    .addr(multiplexer_1_out), .din(\Accum_сложение_q ), .data(ram_1_data), .clk(and_2_out));  // open: str, sel, ld, clr
  Register #(.width(4)) \u_Адрес  (.D(ram_1_data[3:0]), .Q(\Адрес_q ), .clk(not_2_out));  // open: en, clr
  Register #(.trigger("falling")) \u_Промежуточный_результат  (
    .D(ram_1_data), .Q(\Промежуточный_результат_q ), .clk(and_3_out));  // open: en, clr
  and and_3 (and_3_out, \Команда_q [0], not_2_out);
  Register #(.width(4)) \u_Команда  (.D(ram_1_data[7:4]), .Q(\Команда_q ), .clk(not_2_out));  // open: en, clr
  Adder adder_1 (.a(\Accum_сложение_q ), .b(\Промежуточный_результат_q ), .out(adder_1_out));  // open: cin, cout
  Multiplexer #(.width(8)) multiplexer_2 (
    .in0(adder_1_out), .in1(\Промежуточный_результат_q ), .out(multiplexer_2_out), .sel(\Команда_q [2]));  // open: en
  Register #(.trigger("falling")) \Accum_сложение  (
    .D(multiplexer_2_out), .Q(\Accum_сложение_q ), .clk(clock_1_out));  // open: en, clr
  // Probe on \Accum_сложение_q 

  // Notes on the sheet:
  //   1 цифра - Номер команды
  //   0 - переход обратно
  //   1 - сложение
  //   2 - запись в ОЗУ
  //   2 цифра - Адрес ячейки
endmodule
