// Logisim project Гарвардская архитектура.circ as structural Verilog: 1 circuit, main circuit main
module main (
  input  [3:0] DATA_IN,
  input  [11:0] in_2,
  output ACC_0,
  output ACC_0_2,
  output [3:0] out_5
);

  wire and_1_out, and_2_out, and_3_out, clock_1_out, not_1_out, not_2_out, or_1_out;
  wire [3:0] adder_1_out, multiplexer_1_out, ram_1_data, ram_2_data, subtractor_1_out, \акум_q , \Счетчик_q ;
  wire [11:4] ram_1_data_2;

  and and_1 (and_1_out, ram_1_data_2[5], ACC_0);
  and and_2 (and_2_out, ram_1_data_2[4], ACC_0_2);
  or or_1 (or_1_out, ram_1_data_2[6], and_1_out, and_2_out);
  Counter #(.width(4), .max('hf)) \u_Счетчик  (
    .load(or_1_out), .D(ram_1_data), .count(not_1_out), .Q(\Счетчик_q ), .clk(clock_1_out));  // open: carry, clr
  not not_1 (not_1_out, or_1_out);
  Clock clock_1 (.out(clock_1_out));
  RAM #(.addrWidth(4), .dataWidth(12), .bus("separate")) ram_1 (
    .addr(\Счетчик_q ), .din(in_2), .data({ram_1_data_2, ram_1_data}));  // open: str, sel, clk, ld, clr
  not not_2 (not_2_out, clock_1_out);
  and and_3 (and_3_out, ram_1_data_2[10], not_2_out);
  RAM #(.addrWidth(4), .dataWidth(4), .bus("separate")) ram_2 (
    .addr(ram_1_data), .din(\акум_q ), .data(ram_2_data), .clk(ram_1_data_2[11]));  // open: str, sel, ld, clr
  Adder #(.width(4)) adder_1 (.a(\акум_q ), .b(ram_2_data), .out(adder_1_out));  // open: cin, cout
  Subtractor #(.width(4)) subtractor_1 (.a(\акум_q ), .b(ram_2_data), .out(subtractor_1_out));  // open: bin, bout
  Register #(.width(4), .trigger("falling")) \u_акум  (
    .D(multiplexer_1_out), .Q(\акум_q ), .clk(and_3_out));  // open: en, clr
  Multiplexer #(.select(2), .width(4)) multiplexer_1 (
    .in0(DATA_IN), .in1(adder_1_out), .in2(subtractor_1_out), .in3(ram_2_data), .out(multiplexer_1_out),
    .sel(ram_1_data_2[8:7]));  // open: en
  // Probe on ram_1_data_2[8:7]
  Register #(.width(4)) \u_регистр_data_out_выводит_числа  (
    .D(\акум_q ), .Q(out_5), .clk(ram_1_data_2[9]));  // open: en, clr
  nor nor_1 (ACC_0, \акум_q [0], \акум_q [1], \акум_q [2], \акум_q [3]);
  not not_3 (ACC_0_2, \акум_q [3]);

  // Notes on the sheet:
  //   ADD-48 - Сложить
  //   SUB-50 - Вычесть
  //   STA-80 - Сохранить из ACC по адресу X
  //   INP-40 - Выводит значение из DATA IN
  //   OUT-20 - Записывает регистр
  //   Команды
  //   LDA-58 - Загрузить из ОЗУ адреса X в ACC
  //   BRA-04 - Безусловный переход в ячейку с адресом X
  //   BRZ-02 - Переход в ячейчку с адресом X если ACC=0
  //   BRP-01 - Переход в ячейчку с адресом X если ACC=/0
  //   Первые 2 цифры - адрес
  //   Последняя - номер ячейки данных
  //   данные
endmodule
